// Logisim project Processador NAV - Didático.circ as structural Verilog: 11 circuits, main circuit Processador
module COA (
  input  nA,
  input  nB,
  input  [2:0] SELETOR,
  input  A,
  input  B,
  input  Cin,
  input  CinShiftE,
  input  CinShiftD,
  output S,
  output Cout,
  output CoutShiftE,
  output CoutShiftD
);

  wire adder_1_cout, adder_1_out, and_1_out, multiplexer_1_out, multiplexer_2_out, not_1_out, not_2_out,
       or_1_out, subtractor_1_bout, subtractor_1_out, xnor_1_out, xor_1_out;

  Multiplexer multiplexer_1 (.in0(A), .in1(not_1_out), .out(multiplexer_1_out), .sel(nA));  // open: en
  not not_1 (not_1_out, A);
  Multiplexer multiplexer_2 (.in0(B), .in1(not_2_out), .out(multiplexer_2_out), .sel(nB));  // open: en
  not not_2 (not_2_out, B);
  and and_1 (and_1_out, multiplexer_1_out, multiplexer_2_out);
  or or_1 (or_1_out, multiplexer_1_out, multiplexer_2_out);
  xor xor_1 (xor_1_out, multiplexer_1_out, multiplexer_2_out);
  xnor xnor_1 (xnor_1_out, multiplexer_1_out, multiplexer_2_out);
  Adder #(.width(1)) adder_1 (
    .a(multiplexer_1_out), .b(multiplexer_2_out), .out(adder_1_out), .cin(Cin), .cout(adder_1_cout));
  Subtractor #(.width(1)) subtractor_1 (
    .a(multiplexer_1_out), .b(multiplexer_2_out), .out(subtractor_1_out), .bin(Cin), .bout(subtractor_1_bout));
  Multiplexer #(.select(3)) multiplexer_3 (
    .in0(and_1_out), .in1(or_1_out), .in2(xor_1_out), .in3(xnor_1_out), .in4(adder_1_out),
    .in5(subtractor_1_out), .in6(CinShiftE), .in7(CinShiftD), .out(S), .sel(SELETOR));  // open: en
  Multiplexer #(.select(3)) multiplexer_4 (
    .in0(1'b0), .in1(1'b0), .in2(1'b0), .in3(1'b0), .in4(adder_1_cout), .in5(subtractor_1_bout), .in6(1'b0),
    .in7(1'b0), .out(Cout), .sel(SELETOR));  // open: en
  Multiplexer #(.select(3)) multiplexer_5 (
    .in0(1'b0), .in1(1'b0), .in2(1'b0), .in3(1'b0), .in4(1'b0), .in5(1'b0), .in6(A), .in7(1'b0),
    .out(CoutShiftE), .sel(SELETOR));  // open: en
  Multiplexer #(.select(3)) multiplexer_6 (
    .in0(1'b0), .in1(1'b0), .in2(1'b0), .in3(1'b0), .in4(1'b0), .in5(1'b0), .in6(1'b0), .in7(A),
    .out(CoutShiftD), .sel(SELETOR));  // open: en

  // Notes on the sheet:
  //   000: AND
  //   001: OR
  //   010: XOR
  //   011: XNOR
  //   100: SOMA
  //   101: SUB
  //   110: SHIFT E
  //   111: SHIFT D
endmodule

module UOA (
  input  [4:0] SELETOR,
  input  [7:0] A,
  input  [7:0] B,
  output OVERFLOW,
  output [7:0] S
);

  wire coa_1_cout, coa_1_coutshifte, coa_2_cout, coa_2_coutshifte, coa_3_cout, coa_3_coutshiftd,
       coa_3_coutshifte, coa_4_cout, coa_4_coutshiftd, coa_4_coutshifte, coa_5_cout, coa_5_coutshiftd,
       coa_5_coutshifte, coa_6_cout, coa_6_coutshiftd, coa_6_coutshifte, coa_7_cout, coa_7_coutshiftd,
       coa_8_coutshiftd;

  COA coa_1 (
    .S(S[0]), .Cout(coa_1_cout), .A(A[0]), .Cin(1'b0), .SELETOR(SELETOR[2:0]), .CoutShiftE(coa_1_coutshifte),
    .CinShiftE(1'b0), .CinShiftD(coa_3_coutshiftd), .B(B[0]), .nA(SELETOR[4]), .nB(SELETOR[3]));  // open: CoutShiftD
  COA coa_2 (
    .S(S[1]), .Cout(coa_2_cout), .A(A[1]), .Cin(coa_1_cout), .SELETOR(SELETOR[2:0]),
    .CoutShiftE(coa_2_coutshifte), .CinShiftE(1'b0), .CinShiftD(coa_4_coutshiftd), .B(B[1]), .nA(SELETOR[4]),
    .nB(SELETOR[3]));  // open: CoutShiftD
  COA coa_3 (
    .S(S[2]), .Cout(coa_3_cout), .A(A[2]), .Cin(coa_2_cout), .SELETOR(SELETOR[2:0]),
    .CoutShiftE(coa_3_coutshifte), .CinShiftE(coa_1_coutshifte), .CinShiftD(coa_5_coutshiftd),
    .CoutShiftD(coa_3_coutshiftd), .B(B[2]), .nA(SELETOR[4]), .nB(SELETOR[3]));
  COA coa_4 (
    .S(S[3]), .Cout(coa_4_cout), .A(A[3]), .Cin(coa_3_cout), .SELETOR(SELETOR[2:0]),
    .CoutShiftE(coa_4_coutshifte), .CinShiftE(coa_2_coutshifte), .CinShiftD(coa_6_coutshiftd),
    .CoutShiftD(coa_4_coutshiftd), .B(B[3]), .nA(SELETOR[4]), .nB(SELETOR[3]));
  COA coa_5 (
    .S(S[4]), .Cout(coa_5_cout), .A(A[4]), .Cin(coa_4_cout), .SELETOR(SELETOR[2:0]),
    .CoutShiftE(coa_5_coutshifte), .CinShiftE(coa_3_coutshifte), .CinShiftD(coa_7_coutshiftd),
    .CoutShiftD(coa_5_coutshiftd), .B(B[4]), .nA(SELETOR[4]), .nB(SELETOR[3]));
  COA coa_6 (
    .S(S[5]), .Cout(coa_6_cout), .A(A[5]), .Cin(coa_5_cout), .SELETOR(SELETOR[2:0]),
    .CoutShiftE(coa_6_coutshifte), .CinShiftE(coa_4_coutshifte), .CinShiftD(coa_8_coutshiftd),
    .CoutShiftD(coa_6_coutshiftd), .B(B[5]), .nA(SELETOR[4]), .nB(SELETOR[3]));
  COA coa_7 (
    .S(S[6]), .Cout(coa_7_cout), .A(A[6]), .Cin(coa_6_cout), .SELETOR(SELETOR[2:0]),
    .CinShiftE(coa_5_coutshifte), .CinShiftD(1'b0), .CoutShiftD(coa_7_coutshiftd), .B(B[6]), .nA(SELETOR[4]),
    .nB(SELETOR[3]));  // open: CoutShiftE
  COA coa_8 (
    .S(S[7]), .Cout(OVERFLOW), .A(A[7]), .Cin(coa_7_cout), .SELETOR(SELETOR[2:0]),
    .CinShiftE(coa_6_coutshifte), .CinShiftD(1'b0), .CoutShiftD(coa_8_coutshiftd), .B(B[7]), .nA(SELETOR[4]),
    .nB(SELETOR[3]));  // open: CoutShiftE

  // Notes on the sheet:
  //   00000: E
  //   00001: OU
  //   00010: XOR
  //   00011: XNOR
  //   11000: NÃO OU
  //   11001: NÃO E
  //   10100: NÂO
  //   00100: SOMA
  //   00101: SUB
  //   00110: SHIF E. 
  //   00111: SHIF D.
endmodule

module Processador (
  input  LOAD,
  input  [15:0] Ln0,
  input  [15:0] Ln1,
  input  [15:0] Ln2,
  input  [15:0] Ln3,
  input  [15:0] Ln4,
  input  [15:0] Ln5,
  input  [15:0] Ln6,
  input  RESET,
  input  [15:0] Ln7,
  input  [15:0] Ln8,
  input  [15:0] Ln9,
  input  [15:0] Ln10,
  input  [15:0] Ln11,
  input  [15:0] Ln12,
  input  [15:0] Ln13,
  input  [15:0] Ln14,
  input  [15:0] Ln15,
  output [7:0] PRINT
);

  wire clock_1_out, demultiplexer_1_out0, demultiplexer_1_out1, demultiplexer_1_out2, demultiplexer_1_out3,
       demultiplexer_1_out4, demultiplexer_1_out5, demultiplexer_1_out6, demultiplexer_1_out7,
       demultiplexer_1_out8, demultiplexer_1_out9, demultiplexer_1_out10, demultiplexer_1_out11,
       demultiplexer_1_out12, demultiplexer_1_out13, demultiplexer_1_out14, demultiplexer_1_out15, or_1_out,
       unic_1_clock_mem, unic_1_colck_br, unic_1_ctr_br, unic_1_ctr_mem, unic_1_ctr_uol, unic_1_jump,
       unic_1_out, uoa_2_overflow, uol_1_boolean;
  wire [1:0] unic_1_end1, unic_1_end2, unic_1_muoa, unic_1_muva;
  wire [2:0] unic_1_uol_op;
  wire [3:0] \pc_1_endereço_atual , pc_1_valor;
  wire [4:0] unic_1_uoa_op;
  wire [7:0] banco_de_registradores_1_out_8, banco_de_registradores_1_out_10,
       banco_de_registradores_1_out_11, banco_de_registradores_1_out_13, banco_de_registradores_1_r1,
       banco_de_registradores_1_r2, \memória_ram_1_output , \memória_rom_1_ult_op , multiplexer_1_out,
       multiplexer_2_out, pc_1_instru, uoa_2_s;
  wire [7:4] pc_1_valor_2;

  Demultiplexer #(.select(4)) demultiplexer_1 (
    .out0(demultiplexer_1_out0), .out1(demultiplexer_1_out1), .out2(demultiplexer_1_out2),
    .out3(demultiplexer_1_out3), .out4(demultiplexer_1_out4), .out5(demultiplexer_1_out5),
    .out6(demultiplexer_1_out6), .out7(demultiplexer_1_out7), .out8(demultiplexer_1_out8),
    .out9(demultiplexer_1_out9), .out10(demultiplexer_1_out10), .out11(demultiplexer_1_out11),
    .out12(demultiplexer_1_out12), .out13(demultiplexer_1_out13), .out14(demultiplexer_1_out14),
    .out15(demultiplexer_1_out15), .in(1'b1), .sel(\pc_1_endereço_atual ));  // open: en
  LED led_1 (.in(demultiplexer_1_out0));
  LED led_2 (.in(demultiplexer_1_out1));
  LED led_3 (.in(demultiplexer_1_out2));
  LED led_4 (.in(demultiplexer_1_out3));
  LED led_5 (.in(demultiplexer_1_out4));
  LED led_6 (.in(demultiplexer_1_out5));
  LED led_7 (.in(demultiplexer_1_out6));
  LED led_8 (.in(demultiplexer_1_out7));
  LED led_9 (.in(demultiplexer_1_out8));
  LED led_10 (.in(demultiplexer_1_out9));
  LED led_11 (.in(demultiplexer_1_out10));
  LED led_12 (.in(demultiplexer_1_out11));
  LED led_13 (.in(demultiplexer_1_out12));
  LED led_14 (.in(demultiplexer_1_out13));
  LED led_15 (.in(demultiplexer_1_out14));
  LED led_16 (.in(demultiplexer_1_out15));
  PC pc_1 (
    .CLOCK(clock_1_out), .in_5(Ln0), .in_6(Ln1), .in_7(Ln2), .in_8(Ln3), .in_9(Ln4), .in_10(Ln5),
    .in_11(Ln6), .in_12(Ln7), .in_13(Ln8), .in_14(Ln9), .in_15(Ln10), .in_16(Ln11), .in_17(Ln12),
    .in_18(Ln13), .in_19(Ln14), .in_20(Ln15), .LOAD(LOAD), .JUMP(or_1_out), .JUMP_END(pc_1_valor),
    .INSTRU(pc_1_instru), .VALOR({pc_1_valor_2, pc_1_valor}), .\ENDEREÇO_ATUAL (\pc_1_endereço_atual ));
  Clock clock_1 (.out(clock_1_out));
  or or_1 (or_1_out, uol_1_boolean, unic_1_jump);
  // Probe on \memória_rom_1_ult_op 
  \Memória_ROM  \memória_rom_1  (
    .ULT_OP(\memória_rom_1_ult_op ), .RESET(RESET), .ATUAL_OP(pc_1_instru), .CLOCK(clock_1_out));  // open: SET
  UOA uoa_1 ();  // open: SELETOR, A, B, OVERFLOW, S
  Multiplexer #(.select(2), .width(8)) multiplexer_1 (
    .in0({pc_1_valor_2, pc_1_valor}), .in1(uoa_2_s), .in2(\memória_ram_1_output ), .out(multiplexer_1_out),
    .sel(unic_1_muva));  // open: in3, en
  UNIC unic_1 (
    .CLOCK(clock_1_out), .OP(pc_1_instru), .COLCK_BR(unic_1_colck_br), .END1(unic_1_end1),
    .END2(unic_1_end2), .UOA_OP(unic_1_uoa_op), .Ctr_BR(unic_1_ctr_br), .MUOA(unic_1_muoa),
    .MUVA(unic_1_muva), .CLOCK_MEM(unic_1_clock_mem), .Ctr_MEM(unic_1_ctr_mem), .JUMP(unic_1_jump),
    .UOL_OP(unic_1_uol_op), .Ctr_UOL(unic_1_ctr_uol), .OUT(unic_1_out));
  // Probe on banco_de_registradores_1_out_8
  // Probe on banco_de_registradores_1_out_10
  // Probe on banco_de_registradores_1_out_11
  // Probe on banco_de_registradores_1_out_13
  Banco_de_Registradores banco_de_registradores_1 (
    .\ENDEREÇO_R1 (unic_1_end1), .\ENDEREÇO_R2 (unic_1_end2), .R1(banco_de_registradores_1_r1),
    .R2(banco_de_registradores_1_r2), .ESC_0_LER_1(unic_1_ctr_br), .INPUT(multiplexer_1_out),
    .CLOCK(unic_1_colck_br), .RESET(RESET), .out_8(banco_de_registradores_1_out_8),
    .out_11(banco_de_registradores_1_out_11), .out_10(banco_de_registradores_1_out_10),
    .out_13(banco_de_registradores_1_out_13));  // open: SET
  \Memória_RAM  \memória_ram_1  (
    .OUTPUT(\memória_ram_1_output ), .ARRAY(unic_1_end2), .RESET(RESET), .INPUT(multiplexer_1_out),
    .LER_0_ESC_1(unic_1_ctr_mem), .CLOCK(unic_1_clock_mem), .INDEX({pc_1_valor_2, pc_1_valor}));  // open: SET
  Multiplexer #(.select(2), .width(8)) multiplexer_2 (
    .in0({8{1'b0}}), .in1({pc_1_valor_2, pc_1_valor}), .in2(banco_de_registradores_1_r2), .in3({8{1'b0}}),
    .out(multiplexer_2_out), .sel(unic_1_muoa));  // open: en
  UOA uoa_2 (
    .SELETOR(unic_1_uoa_op), .A(banco_de_registradores_1_r1), .B(multiplexer_2_out),
    .OVERFLOW(uoa_2_overflow), .S(uoa_2_s));
  // Probe on banco_de_registradores_1_r1
  // Probe on multiplexer_2_out
  // Probe on uoa_2_s
  UOL uol_1 (
    .BOOLEAN(uol_1_boolean), .L_INPUT(uoa_2_s), .OVERFLOW(uoa_2_overflow), .SELETOR(unic_1_uol_op),
    .CLOCK(unic_1_ctr_uol));
  LED led_17 (.in(unic_1_out));
  Multiplexer #(.width(8)) multiplexer_3 (.in0({8{1'b0}}), .in1(uoa_2_s), .out(PRINT), .sel(unic_1_out));  // open: en

  // Notes on the sheet:
  //   MUVA
  //   MUOA
endmodule

module \Valor_de_Memória_8_bits  (
  input  CLOCK,
  input  SET,
  input  RESET,
  input  [7:0] INPUT,
  output [7:0] OUTPUT
);

  D_Flip_Flop d_ff_1 (.clk(CLOCK), .D(INPUT[0]), .Q(OUTPUT[0]), .preset(SET), .reset(RESET));  // open: Qn, en
  D_Flip_Flop d_ff_2 (.clk(CLOCK), .D(INPUT[1]), .Q(OUTPUT[1]), .preset(SET), .reset(RESET));  // open: Qn, en
  D_Flip_Flop d_ff_3 (.clk(CLOCK), .D(INPUT[2]), .Q(OUTPUT[2]), .preset(SET), .reset(RESET));  // open: Qn, en
  D_Flip_Flop d_ff_4 (.clk(CLOCK), .D(INPUT[3]), .Q(OUTPUT[3]), .preset(SET), .reset(RESET));  // open: Qn, en
  D_Flip_Flop d_ff_5 (.clk(CLOCK), .D(INPUT[4]), .Q(OUTPUT[4]), .preset(SET), .reset(RESET));  // open: Qn, en
  D_Flip_Flop d_ff_6 (.clk(CLOCK), .D(INPUT[5]), .Q(OUTPUT[5]), .preset(SET), .reset(RESET));  // open: Qn, en
  D_Flip_Flop d_ff_7 (.clk(CLOCK), .D(INPUT[6]), .Q(OUTPUT[6]), .preset(SET), .reset(RESET));  // open: Qn, en
  D_Flip_Flop d_ff_8 (.clk(CLOCK), .D(INPUT[7]), .Q(OUTPUT[7]), .preset(SET), .reset(RESET));  // open: Qn, en
endmodule

module \Memória_ROM  (
  input  RESET,
  input  SET,
  input  [7:0] ATUAL_OP,
  input  CLOCK,
  output [7:0] ULT_OP
);

  wire demultiplexer_1_out0, demultiplexer_1_out1, demultiplexer_1_out2, demultiplexer_1_out3,
       demultiplexer_1_out4, demultiplexer_1_out5, demultiplexer_1_out6, demultiplexer_1_out7,
       demultiplexer_1_out8, demultiplexer_1_out9, demultiplexer_1_out10, demultiplexer_1_out11,
       demultiplexer_1_out12, demultiplexer_1_out13, demultiplexer_1_out14, demultiplexer_1_out15;
  wire [3:0] counter_1_q, subtractor_1_out;
  wire [7:0] \valor_de_memória_8_bits_1_output , \valor_de_memória_8_bits_2_output ,
       \valor_de_memória_8_bits_3_output , \valor_de_memória_8_bits_4_output ,
       \valor_de_memória_8_bits_5_output , \valor_de_memória_8_bits_6_output ,
       \valor_de_memória_8_bits_7_output , \valor_de_memória_8_bits_8_output ,
       \valor_de_memória_8_bits_9_output , \valor_de_memória_8_bits_10_output ,
       \valor_de_memória_8_bits_11_output , \valor_de_memória_8_bits_12_output ,
       \valor_de_memória_8_bits_13_output , \valor_de_memória_8_bits_14_output ,
       \valor_de_memória_8_bits_15_output , \valor_de_memória_8_bits_16_output ;

  Counter #(.width(4), .max('hf)) counter_1 (
    .count(1'b1), .Q(counter_1_q), .clk(CLOCK), .clr(RESET));  // open: load, D, carry
  Demultiplexer #(.select(4)) demultiplexer_1 (
    .out0(demultiplexer_1_out0), .out1(demultiplexer_1_out1), .out2(demultiplexer_1_out2),
    .out3(demultiplexer_1_out3), .out4(demultiplexer_1_out4), .out5(demultiplexer_1_out5),
    .out6(demultiplexer_1_out6), .out7(demultiplexer_1_out7), .out8(demultiplexer_1_out8),
    .out9(demultiplexer_1_out9), .out10(demultiplexer_1_out10), .out11(demultiplexer_1_out11),
    .out12(demultiplexer_1_out12), .out13(demultiplexer_1_out13), .out14(demultiplexer_1_out14),
    .out15(demultiplexer_1_out15), .in(1'b1), .sel(counter_1_q));  // open: en
  Subtractor #(.width(4)) subtractor_1 (.a(counter_1_q), .b(4'b0001), .out(subtractor_1_out));  // open: bin, bout
  \Valor_de_Memória_8_bits  \valor_de_memória_8_bits_1  (
    .INPUT(ATUAL_OP), .SET(SET), .CLOCK(demultiplexer_1_out0), .RESET(RESET),
    .OUTPUT(\valor_de_memória_8_bits_1_output ));
  \Valor_de_Memória_8_bits  \valor_de_memória_8_bits_2  (
    .INPUT(ATUAL_OP), .SET(SET), .CLOCK(demultiplexer_1_out1), .RESET(RESET),
    .OUTPUT(\valor_de_memória_8_bits_2_output ));
  \Valor_de_Memória_8_bits  \valor_de_memória_8_bits_3  (
    .INPUT(ATUAL_OP), .SET(SET), .CLOCK(demultiplexer_1_out2), .RESET(RESET),
    .OUTPUT(\valor_de_memória_8_bits_3_output ));
  \Valor_de_Memória_8_bits  \valor_de_memória_8_bits_4  (
    .INPUT(ATUAL_OP), .SET(SET), .CLOCK(demultiplexer_1_out3), .RESET(RESET),
    .OUTPUT(\valor_de_memória_8_bits_4_output ));
  \Valor_de_Memória_8_bits  \valor_de_memória_8_bits_5  (
    .INPUT(ATUAL_OP), .SET(SET), .CLOCK(demultiplexer_1_out4), .RESET(RESET),
    .OUTPUT(\valor_de_memória_8_bits_5_output ));
  \Valor_de_Memória_8_bits  \valor_de_memória_8_bits_6  (
    .INPUT(ATUAL_OP), .SET(SET), .CLOCK(demultiplexer_1_out5), .RESET(RESET),
    .OUTPUT(\valor_de_memória_8_bits_6_output ));
  \Valor_de_Memória_8_bits  \valor_de_memória_8_bits_7  (
    .INPUT(ATUAL_OP), .SET(SET), .CLOCK(demultiplexer_1_out6), .RESET(RESET),
    .OUTPUT(\valor_de_memória_8_bits_7_output ));
  \Valor_de_Memória_8_bits  \valor_de_memória_8_bits_8  (
    .INPUT(ATUAL_OP), .SET(SET), .CLOCK(demultiplexer_1_out7), .RESET(RESET),
    .OUTPUT(\valor_de_memória_8_bits_8_output ));
  \Valor_de_Memória_8_bits  \valor_de_memória_8_bits_9  (
    .INPUT(ATUAL_OP), .SET(SET), .CLOCK(demultiplexer_1_out8), .RESET(RESET),
    .OUTPUT(\valor_de_memória_8_bits_9_output ));
  \Valor_de_Memória_8_bits  \valor_de_memória_8_bits_10  (
    .INPUT(ATUAL_OP), .SET(SET), .CLOCK(demultiplexer_1_out9), .RESET(RESET),
    .OUTPUT(\valor_de_memória_8_bits_10_output ));
  \Valor_de_Memória_8_bits  \valor_de_memória_8_bits_11  (
    .INPUT(ATUAL_OP), .SET(SET), .CLOCK(demultiplexer_1_out10), .RESET(RESET),
    .OUTPUT(\valor_de_memória_8_bits_11_output ));
  \Valor_de_Memória_8_bits  \valor_de_memória_8_bits_12  (
    .INPUT(ATUAL_OP), .SET(SET), .CLOCK(demultiplexer_1_out11), .RESET(RESET),
    .OUTPUT(\valor_de_memória_8_bits_12_output ));
  \Valor_de_Memória_8_bits  \valor_de_memória_8_bits_13  (
    .INPUT(ATUAL_OP), .SET(SET), .CLOCK(demultiplexer_1_out12), .RESET(RESET),
    .OUTPUT(\valor_de_memória_8_bits_13_output ));
  \Valor_de_Memória_8_bits  \valor_de_memória_8_bits_14  (
    .INPUT(ATUAL_OP), .SET(SET), .CLOCK(demultiplexer_1_out13), .RESET(RESET),
    .OUTPUT(\valor_de_memória_8_bits_14_output ));
  \Valor_de_Memória_8_bits  \valor_de_memória_8_bits_15  (
    .INPUT(ATUAL_OP), .SET(SET), .CLOCK(demultiplexer_1_out14), .RESET(RESET),
    .OUTPUT(\valor_de_memória_8_bits_15_output ));
  \Valor_de_Memória_8_bits  \valor_de_memória_8_bits_16  (
    .INPUT(ATUAL_OP), .SET(SET), .CLOCK(demultiplexer_1_out15), .RESET(RESET),
    .OUTPUT(\valor_de_memória_8_bits_16_output ));
  // Probe on \valor_de_memória_8_bits_1_output 
  // Probe on \valor_de_memória_8_bits_2_output 
  // Probe on \valor_de_memória_8_bits_3_output 
  // Probe on \valor_de_memória_8_bits_4_output 
  // Probe on \valor_de_memória_8_bits_5_output 
  // Probe on \valor_de_memória_8_bits_6_output 
  // Probe on \valor_de_memória_8_bits_7_output 
  // Probe on \valor_de_memória_8_bits_8_output 
  // Probe on \valor_de_memória_8_bits_9_output 
  // Probe on \valor_de_memória_8_bits_10_output 
  // Probe on \valor_de_memória_8_bits_11_output 
  // Probe on \valor_de_memória_8_bits_12_output 
  // Probe on \valor_de_memória_8_bits_13_output 
  // Probe on \valor_de_memória_8_bits_14_output 
  // Probe on \valor_de_memória_8_bits_15_output 
  // Probe on \valor_de_memória_8_bits_16_output 
  // Probe on subtractor_1_out
  Multiplexer #(.select(4), .width(8)) multiplexer_1 (
    .in0(\valor_de_memória_8_bits_1_output ), .in1(\valor_de_memória_8_bits_2_output ),
    .in2(\valor_de_memória_8_bits_3_output ), .in3(\valor_de_memória_8_bits_4_output ),
    .in4(\valor_de_memória_8_bits_5_output ), .in5(\valor_de_memória_8_bits_6_output ),
    .in6(\valor_de_memória_8_bits_7_output ), .in7(\valor_de_memória_8_bits_8_output ),
    .in8(\valor_de_memória_8_bits_9_output ), .in9(\valor_de_memória_8_bits_10_output ),
    .in10(\valor_de_memória_8_bits_11_output ), .in11(\valor_de_memória_8_bits_12_output ),
    .in12(\valor_de_memória_8_bits_13_output ), .in13(\valor_de_memória_8_bits_14_output ),
    .in14(\valor_de_memória_8_bits_15_output ), .in15(\valor_de_memória_8_bits_16_output ), .out(ULT_OP),
    .sel(subtractor_1_out));  // open: en
endmodule

module Banco_de_Registradores (
  input  ESC_0_LER_1,
  input  RESET,
  input  [7:0] INPUT,
  input  SET,
  input  [1:0] \ENDEREÇO_R1 ,
  input  CLOCK,
  input  [1:0] \ENDEREÇO_R2 ,
  output [7:0] out_8,
  output [7:0] R1,
  output [7:0] out_10,
  output [7:0] out_11,
  output [7:0] R2,
  output [7:0] out_13
);

  wire demultiplexer_1_out0, demultiplexer_1_out1, demultiplexer_1_out2, demultiplexer_1_out3,
       multiplexer_1_out;

  Multiplexer multiplexer_1 (.in0(CLOCK), .in1(1'b0), .out(multiplexer_1_out), .sel(ESC_0_LER_1));  // open: en
  Demultiplexer #(.select(2)) demultiplexer_1 (
    .out0(demultiplexer_1_out0), .out1(demultiplexer_1_out1), .out2(demultiplexer_1_out2),
    .out3(demultiplexer_1_out3), .in(multiplexer_1_out), .sel(\ENDEREÇO_R1 ));  // open: en
  \Valor_de_Memória_8_bits  \valor_de_memória_8_bits_1  (
    .INPUT(INPUT), .SET(SET), .CLOCK(demultiplexer_1_out0), .RESET(RESET), .OUTPUT(out_8));
  \Valor_de_Memória_8_bits  \valor_de_memória_8_bits_2  (
    .INPUT(INPUT), .SET(SET), .CLOCK(demultiplexer_1_out1), .RESET(RESET), .OUTPUT(out_10));
  \Valor_de_Memória_8_bits  \valor_de_memória_8_bits_3  (
    .INPUT(INPUT), .SET(SET), .CLOCK(demultiplexer_1_out2), .RESET(RESET), .OUTPUT(out_11));
  \Valor_de_Memória_8_bits  \valor_de_memória_8_bits_4  (
    .INPUT(INPUT), .SET(SET), .CLOCK(demultiplexer_1_out3), .RESET(RESET), .OUTPUT(out_13));
  Multiplexer #(.select(2), .width(8)) multiplexer_2 (
    .in0(out_8), .in1(out_10), .in2(out_11), .in3(out_13), .out(R1), .sel(\ENDEREÇO_R1 ));  // open: en
  Multiplexer #(.select(2), .width(8)) multiplexer_3 (
    .in0(out_8), .in1(out_10), .in2(out_11), .in3(out_13), .out(R2), .sel(\ENDEREÇO_R2 ));  // open: en
endmodule

module UNIC (
  input  [7:0] OP,
  input  CLOCK,
  output [1:0] MUOA,
  output COLCK_BR,
  output [1:0] END2,
  output [1:0] END1,
  output CLOCK_MEM,
  output [4:0] UOA_OP,
  output Ctr_BR,
  output [2:0] UOL_OP,
  output [1:0] MUVA,
  output OUT,
  output Ctr_MEM,
  output Ctr_UOL,
  output JUMP
);

  wire demultiplexer_1_out1, demultiplexer_1_out2, demultiplexer_1_out3, demultiplexer_1_out4,
       demultiplexer_1_out5, demultiplexer_1_out8, demultiplexer_1_out9, demultiplexer_1_out10,
       demultiplexer_1_out11, demultiplexer_1_out12, demultiplexer_1_out13, demultiplexer_1_out14, or_1_out,
       or_3_out, or_4_out, or_7_out, or_12_out;

  Demultiplexer #(.select(4)) demultiplexer_1 (
    .out0(OUT), .out1(demultiplexer_1_out1), .out2(demultiplexer_1_out2), .out3(demultiplexer_1_out3),
    .out4(demultiplexer_1_out4), .out5(demultiplexer_1_out5), .out6(Ctr_MEM), .out7(MUVA[1]),
    .out8(demultiplexer_1_out8), .out9(demultiplexer_1_out9), .out10(demultiplexer_1_out10),
    .out11(demultiplexer_1_out11), .out12(demultiplexer_1_out12), .out13(demultiplexer_1_out13),
    .out14(demultiplexer_1_out14), .out15(JUMP), .in(1'b1), .sel(OP[7:4]));  // open: en
  or or_1 (or_1_out, demultiplexer_1_out3, demultiplexer_1_out5);
  or or_2 (UOA_OP[1], demultiplexer_1_out8, demultiplexer_1_out9);
  or or_3 (or_3_out, demultiplexer_1_out4, demultiplexer_1_out5);
  or or_4 (or_4_out, demultiplexer_1_out10, demultiplexer_1_out11, demultiplexer_1_out12, demultiplexer_1_out13, demultiplexer_1_out14);
  or or_5 (MUOA[1], or_1_out, UOA_OP[1], or_4_out);
  or or_6 (MUOA[0], demultiplexer_1_out2, demultiplexer_1_out4);
  or or_7 (or_7_out, Ctr_MEM, MUVA[1]);
  or or_8 (UOA_OP[0], or_3_out, or_4_out, UOA_OP[1]);
  or or_9 (UOA_OP[2], or_1_out, or_4_out, MUOA[0], or_7_out, OUT);
  or or_10 (MUVA[0], demultiplexer_1_out2, demultiplexer_1_out3, Ctr_MEM, demultiplexer_1_out4, demultiplexer_1_out5);
  or or_11 (Ctr_UOL, demultiplexer_1_out8, demultiplexer_1_out9, demultiplexer_1_out10, demultiplexer_1_out11, demultiplexer_1_out12, demultiplexer_1_out13, demultiplexer_1_out14);
  and and_1 (COLCK_BR, CLOCK, or_12_out);
  or or_12 (or_12_out, demultiplexer_1_out1, MUVA[1], MUVA[0]);
  and and_2 (CLOCK_MEM, CLOCK, Ctr_MEM);
  or or_13 (Ctr_BR, Ctr_MEM, Ctr_UOL);

  assign END1 = OP[3:2];
  assign END2 = OP[1:0];
  assign UOA_OP[4:3] = 2'b00;
  assign UOL_OP = OP[6:4];
endmodule

module \Memória_RAM  (
  input  [7:0] INDEX,
  input  [1:0] ARRAY,
  input  LER_0_ESC_1,
  input  RESET,
  input  [7:0] INPUT,
  input  SET,
  input  CLOCK,
  output [7:0] OUTPUT
);

  wire demultiplexer_1_out0, demultiplexer_1_out1, demultiplexer_1_out2, demultiplexer_1_out3,
       demultiplexer_1_out4, demultiplexer_1_out5, demultiplexer_1_out6, demultiplexer_1_out7,
       demultiplexer_1_out8, demultiplexer_1_out9, demultiplexer_1_out10, demultiplexer_1_out11,
       demultiplexer_1_out12, demultiplexer_1_out13, demultiplexer_1_out14, demultiplexer_1_out15,
       multiplexer_1_out;
  wire [7:0] multiplexer_2_out, \valor_de_memória_8_bits_1_output , \valor_de_memória_8_bits_2_output ,
       \valor_de_memória_8_bits_3_output , \valor_de_memória_8_bits_4_output ,
       \valor_de_memória_8_bits_5_output , \valor_de_memória_8_bits_6_output ,
       \valor_de_memória_8_bits_7_output , \valor_de_memória_8_bits_8_output ,
       \valor_de_memória_8_bits_9_output , \valor_de_memória_8_bits_10_output ,
       \valor_de_memória_8_bits_11_output , \valor_de_memória_8_bits_12_output ,
       \valor_de_memória_8_bits_13_output , \valor_de_memória_8_bits_14_output ,
       \valor_de_memória_8_bits_15_output , \valor_de_memória_8_bits_16_output ;

  Multiplexer multiplexer_1 (.in0(1'b0), .in1(CLOCK), .out(multiplexer_1_out), .sel(LER_0_ESC_1));  // open: en
  Demultiplexer #(.select(4)) demultiplexer_1 (
    .out0(demultiplexer_1_out0), .out1(demultiplexer_1_out1), .out2(demultiplexer_1_out2),
    .out3(demultiplexer_1_out3), .out4(demultiplexer_1_out4), .out5(demultiplexer_1_out5),
    .out6(demultiplexer_1_out6), .out7(demultiplexer_1_out7), .out8(demultiplexer_1_out8),
    .out9(demultiplexer_1_out9), .out10(demultiplexer_1_out10), .out11(demultiplexer_1_out11),
    .out12(demultiplexer_1_out12), .out13(demultiplexer_1_out13), .out14(demultiplexer_1_out14),
    .out15(demultiplexer_1_out15), .in(multiplexer_1_out), .sel({ARRAY, INDEX[1:0]}));  // open: en
  \Valor_de_Memória_8_bits  \valor_de_memória_8_bits_1  (
    .INPUT(INPUT), .SET(SET), .CLOCK(demultiplexer_1_out0), .RESET(RESET),
    .OUTPUT(\valor_de_memória_8_bits_1_output ));
  // Probe on \valor_de_memória_8_bits_1_output 
  \Valor_de_Memória_8_bits  \valor_de_memória_8_bits_2  (
    .INPUT(INPUT), .SET(SET), .CLOCK(demultiplexer_1_out1), .RESET(RESET),
    .OUTPUT(\valor_de_memória_8_bits_2_output ));
  // Probe on \valor_de_memória_8_bits_2_output 
  \Valor_de_Memória_8_bits  \valor_de_memória_8_bits_3  (
    .INPUT(INPUT), .SET(SET), .CLOCK(demultiplexer_1_out2), .RESET(RESET),
    .OUTPUT(\valor_de_memória_8_bits_3_output ));
  // Probe on \valor_de_memória_8_bits_3_output 
  \Valor_de_Memória_8_bits  \valor_de_memória_8_bits_4  (
    .INPUT(INPUT), .SET(SET), .CLOCK(demultiplexer_1_out3), .RESET(RESET),
    .OUTPUT(\valor_de_memória_8_bits_4_output ));
  // Probe on \valor_de_memória_8_bits_4_output 
  \Valor_de_Memória_8_bits  \valor_de_memória_8_bits_5  (
    .INPUT(INPUT), .SET(SET), .CLOCK(demultiplexer_1_out4), .RESET(RESET),
    .OUTPUT(\valor_de_memória_8_bits_5_output ));
  // Probe on \valor_de_memória_8_bits_5_output 
  \Valor_de_Memória_8_bits  \valor_de_memória_8_bits_6  (
    .INPUT(INPUT), .SET(SET), .CLOCK(demultiplexer_1_out5), .RESET(RESET),
    .OUTPUT(\valor_de_memória_8_bits_6_output ));
  // Probe on \valor_de_memória_8_bits_6_output 
  \Valor_de_Memória_8_bits  \valor_de_memória_8_bits_7  (
    .INPUT(INPUT), .SET(SET), .CLOCK(demultiplexer_1_out6), .RESET(RESET),
    .OUTPUT(\valor_de_memória_8_bits_7_output ));
  // Probe on \valor_de_memória_8_bits_7_output 
  \Valor_de_Memória_8_bits  \valor_de_memória_8_bits_8  (
    .INPUT(INPUT), .SET(SET), .CLOCK(demultiplexer_1_out7), .RESET(RESET),
    .OUTPUT(\valor_de_memória_8_bits_8_output ));
  // Probe on \valor_de_memória_8_bits_8_output 
  \Valor_de_Memória_8_bits  \valor_de_memória_8_bits_9  (
    .INPUT(INPUT), .SET(SET), .CLOCK(demultiplexer_1_out8), .RESET(RESET),
    .OUTPUT(\valor_de_memória_8_bits_9_output ));
  // Probe on \valor_de_memória_8_bits_9_output 
  \Valor_de_Memória_8_bits  \valor_de_memória_8_bits_10  (
    .INPUT(INPUT), .SET(SET), .CLOCK(demultiplexer_1_out9), .RESET(RESET),
    .OUTPUT(\valor_de_memória_8_bits_10_output ));
  // Probe on \valor_de_memória_8_bits_10_output 
  \Valor_de_Memória_8_bits  \valor_de_memória_8_bits_11  (
    .INPUT(INPUT), .SET(SET), .CLOCK(demultiplexer_1_out10), .RESET(RESET),
    .OUTPUT(\valor_de_memória_8_bits_11_output ));
  // Probe on \valor_de_memória_8_bits_11_output 
  \Valor_de_Memória_8_bits  \valor_de_memória_8_bits_12  (
    .INPUT(INPUT), .SET(SET), .CLOCK(demultiplexer_1_out11), .RESET(RESET),
    .OUTPUT(\valor_de_memória_8_bits_12_output ));
  // Probe on \valor_de_memória_8_bits_12_output 
  \Valor_de_Memória_8_bits  \valor_de_memória_8_bits_13  (
    .INPUT(INPUT), .SET(SET), .CLOCK(demultiplexer_1_out12), .RESET(RESET),
    .OUTPUT(\valor_de_memória_8_bits_13_output ));
  // Probe on \valor_de_memória_8_bits_13_output 
  \Valor_de_Memória_8_bits  \valor_de_memória_8_bits_14  (
    .INPUT(INPUT), .SET(SET), .CLOCK(demultiplexer_1_out13), .RESET(RESET),
    .OUTPUT(\valor_de_memória_8_bits_14_output ));
  // Probe on \valor_de_memória_8_bits_14_output 
  \Valor_de_Memória_8_bits  \valor_de_memória_8_bits_15  (
    .INPUT(INPUT), .SET(SET), .CLOCK(demultiplexer_1_out14), .RESET(RESET),
    .OUTPUT(\valor_de_memória_8_bits_15_output ));
  // Probe on \valor_de_memória_8_bits_15_output 
  \Valor_de_Memória_8_bits  \valor_de_memória_8_bits_16  (
    .INPUT(INPUT), .SET(SET), .CLOCK(demultiplexer_1_out15), .RESET(RESET),
    .OUTPUT(\valor_de_memória_8_bits_16_output ));
  // Probe on \valor_de_memória_8_bits_16_output 
  Multiplexer #(.select(4), .width(8)) multiplexer_2 (
    .in0(\valor_de_memória_8_bits_1_output ), .in1(\valor_de_memória_8_bits_2_output ),
    .in2(\valor_de_memória_8_bits_3_output ), .in3(\valor_de_memória_8_bits_4_output ),
    .in4(\valor_de_memória_8_bits_5_output ), .in5(\valor_de_memória_8_bits_6_output ),
    .in6(\valor_de_memória_8_bits_7_output ), .in7(\valor_de_memória_8_bits_8_output ),
    .in8(\valor_de_memória_8_bits_9_output ), .in9(\valor_de_memória_8_bits_10_output ),
    .in10(\valor_de_memória_8_bits_11_output ), .in11(\valor_de_memória_8_bits_12_output ),
    .in12(\valor_de_memória_8_bits_13_output ), .in13(\valor_de_memória_8_bits_14_output ),
    .in14(\valor_de_memória_8_bits_15_output ), .in15(\valor_de_memória_8_bits_16_output ),
    .out(multiplexer_2_out), .sel({ARRAY, INDEX[1:0]}));  // open: en
  Multiplexer #(.width(8)) multiplexer_3 (
    .in0(multiplexer_2_out), .in1({8{1'b0}}), .out(OUTPUT), .sel(LER_0_ESC_1));  // open: en
endmodule

module PC (
  input  LOAD,
  input  [3:0] JUMP_END,
  input  JUMP,
  input  CLOCK,
  input  [15:0] in_5,
  input  [15:0] in_6,
  input  [15:0] in_7,
  input  [15:0] in_8,
  input  [15:0] in_9,
  input  [15:0] in_10,
  input  [15:0] in_11,
  input  [15:0] in_12,
  input  [15:0] in_13,
  input  [15:0] in_14,
  input  [15:0] in_15,
  input  [15:0] in_16,
  input  [15:0] in_17,
  input  [15:0] in_18,
  input  [15:0] in_19,
  input  [15:0] in_20,
  output [3:0] \ENDEREÇO_ATUAL ,
  output [7:0] INSTRU,
  output [7:0] VALOR
);

  wire not_1_out, not_2_out;
  wire [15:0] linha_de_comando_16_bits_1_output, linha_de_comando_16_bits_2_output,
       linha_de_comando_16_bits_3_output, linha_de_comando_16_bits_4_output,
       linha_de_comando_16_bits_5_output, linha_de_comando_16_bits_6_output,
       linha_de_comando_16_bits_7_output, linha_de_comando_16_bits_8_output,
       linha_de_comando_16_bits_9_output, linha_de_comando_16_bits_10_output,
       linha_de_comando_16_bits_11_output, linha_de_comando_16_bits_12_output,
       linha_de_comando_16_bits_13_output, linha_de_comando_16_bits_14_output,
       linha_de_comando_16_bits_15_output, linha_de_comando_16_bits_16_output;

  not not_1 (not_1_out, CLOCK);
  Linha_de_Comando_16_bits linha_de_comando_16_bits_1 (
    .INPUT(in_5), .CLOCK(LOAD), .OUTPUT(linha_de_comando_16_bits_1_output));  // open: SET, RESET
  Linha_de_Comando_16_bits linha_de_comando_16_bits_2 (
    .INPUT(in_6), .CLOCK(LOAD), .OUTPUT(linha_de_comando_16_bits_2_output));  // open: SET, RESET
  Linha_de_Comando_16_bits linha_de_comando_16_bits_3 (
    .INPUT(in_7), .CLOCK(LOAD), .OUTPUT(linha_de_comando_16_bits_3_output));  // open: SET, RESET
  Linha_de_Comando_16_bits linha_de_comando_16_bits_4 (
    .INPUT(in_8), .CLOCK(LOAD), .OUTPUT(linha_de_comando_16_bits_4_output));  // open: SET, RESET
  Linha_de_Comando_16_bits linha_de_comando_16_bits_5 (
    .INPUT(in_9), .CLOCK(LOAD), .OUTPUT(linha_de_comando_16_bits_5_output));  // open: SET, RESET
  Linha_de_Comando_16_bits linha_de_comando_16_bits_6 (
    .INPUT(in_10), .CLOCK(LOAD), .OUTPUT(linha_de_comando_16_bits_6_output));  // open: SET, RESET
  Linha_de_Comando_16_bits linha_de_comando_16_bits_7 (
    .INPUT(in_11), .CLOCK(LOAD), .OUTPUT(linha_de_comando_16_bits_7_output));  // open: SET, RESET
  Linha_de_Comando_16_bits linha_de_comando_16_bits_8 (
    .INPUT(in_12), .CLOCK(LOAD), .OUTPUT(linha_de_comando_16_bits_8_output));  // open: SET, RESET
  Linha_de_Comando_16_bits linha_de_comando_16_bits_9 (
    .INPUT(in_13), .CLOCK(LOAD), .OUTPUT(linha_de_comando_16_bits_9_output));  // open: SET, RESET
  Linha_de_Comando_16_bits linha_de_comando_16_bits_10 (
    .INPUT(in_14), .CLOCK(LOAD), .OUTPUT(linha_de_comando_16_bits_10_output));  // open: SET, RESET
  Linha_de_Comando_16_bits linha_de_comando_16_bits_11 (
    .INPUT(in_15), .CLOCK(LOAD), .OUTPUT(linha_de_comando_16_bits_11_output));  // open: SET, RESET
  Linha_de_Comando_16_bits linha_de_comando_16_bits_12 (
    .INPUT(in_16), .CLOCK(LOAD), .OUTPUT(linha_de_comando_16_bits_12_output));  // open: SET, RESET
  Linha_de_Comando_16_bits linha_de_comando_16_bits_13 (
    .INPUT(in_17), .CLOCK(LOAD), .OUTPUT(linha_de_comando_16_bits_13_output));  // open: SET, RESET
  Linha_de_Comando_16_bits linha_de_comando_16_bits_14 (
    .INPUT(in_18), .CLOCK(LOAD), .OUTPUT(linha_de_comando_16_bits_14_output));  // open: SET, RESET
  Linha_de_Comando_16_bits linha_de_comando_16_bits_15 (
    .INPUT(in_19), .CLOCK(LOAD), .OUTPUT(linha_de_comando_16_bits_15_output));  // open: SET, RESET
  Linha_de_Comando_16_bits linha_de_comando_16_bits_16 (
    .INPUT(in_20), .CLOCK(LOAD), .OUTPUT(linha_de_comando_16_bits_16_output));  // open: SET, RESET
  not not_2 (not_2_out, JUMP);
  Counter #(.width(4), .max('hf)) counter_1 (
    .load(JUMP), .D(JUMP_END), .count(not_2_out), .Q(\ENDEREÇO_ATUAL ), .clk(not_1_out));  // open: carry, clr
  Multiplexer #(.select(4), .width(16)) multiplexer_1 (
    .in0(linha_de_comando_16_bits_1_output), .in1(linha_de_comando_16_bits_2_output),
    .in2(linha_de_comando_16_bits_3_output), .in3(linha_de_comando_16_bits_4_output),
    .in4(linha_de_comando_16_bits_5_output), .in5(linha_de_comando_16_bits_6_output),
    .in6(linha_de_comando_16_bits_7_output), .in7(linha_de_comando_16_bits_8_output),
    .in8(linha_de_comando_16_bits_9_output), .in9(linha_de_comando_16_bits_10_output),
    .in10(linha_de_comando_16_bits_11_output), .in11(linha_de_comando_16_bits_12_output),
    .in12(linha_de_comando_16_bits_13_output), .in13(linha_de_comando_16_bits_14_output),
    .in14(linha_de_comando_16_bits_15_output), .in15(linha_de_comando_16_bits_16_output),
    .out({VALOR, INSTRU}), .sel(\ENDEREÇO_ATUAL ));  // open: en
endmodule

module Linha_de_Comando_16_bits (
  input  CLOCK,
  input  SET,
  input  RESET,
  input  [15:0] INPUT,
  output [15:0] OUTPUT
);

  D_Flip_Flop d_ff_1 (.clk(CLOCK), .D(INPUT[0]), .Q(OUTPUT[0]), .preset(SET), .reset(RESET));  // open: Qn, en
  D_Flip_Flop d_ff_2 (.clk(CLOCK), .D(INPUT[1]), .Q(OUTPUT[1]), .preset(SET), .reset(RESET));  // open: Qn, en
  D_Flip_Flop d_ff_3 (.clk(CLOCK), .D(INPUT[2]), .Q(OUTPUT[2]), .preset(SET), .reset(RESET));  // open: Qn, en
  D_Flip_Flop d_ff_4 (.clk(CLOCK), .D(INPUT[3]), .Q(OUTPUT[3]), .preset(SET), .reset(RESET));  // open: Qn, en
  D_Flip_Flop d_ff_5 (.clk(CLOCK), .D(INPUT[4]), .Q(OUTPUT[4]), .preset(SET), .reset(RESET));  // open: Qn, en
  D_Flip_Flop d_ff_6 (.clk(CLOCK), .D(INPUT[5]), .Q(OUTPUT[5]), .preset(SET), .reset(RESET));  // open: Qn, en
  D_Flip_Flop d_ff_7 (.clk(CLOCK), .D(INPUT[6]), .Q(OUTPUT[6]), .preset(SET), .reset(RESET));  // open: Qn, en
  D_Flip_Flop d_ff_8 (.clk(CLOCK), .D(INPUT[7]), .Q(OUTPUT[7]), .preset(SET), .reset(RESET));  // open: Qn, en
  D_Flip_Flop d_ff_9 (.clk(CLOCK), .D(INPUT[8]), .Q(OUTPUT[8]), .preset(SET), .reset(RESET));  // open: Qn, en
  D_Flip_Flop d_ff_10 (.clk(CLOCK), .D(INPUT[9]), .Q(OUTPUT[9]), .preset(SET), .reset(RESET));  // open: Qn, en
  D_Flip_Flop d_ff_11 (.clk(CLOCK), .D(INPUT[10]), .Q(OUTPUT[10]), .preset(SET), .reset(RESET));  // open: Qn, en
  D_Flip_Flop d_ff_12 (.clk(CLOCK), .D(INPUT[11]), .Q(OUTPUT[11]), .preset(SET), .reset(RESET));  // open: Qn, en
  D_Flip_Flop d_ff_13 (.clk(CLOCK), .D(INPUT[12]), .Q(OUTPUT[12]), .preset(SET), .reset(RESET));  // open: Qn, en
  D_Flip_Flop d_ff_14 (.clk(CLOCK), .D(INPUT[13]), .Q(OUTPUT[13]), .preset(SET), .reset(RESET));  // open: Qn, en
  D_Flip_Flop d_ff_15 (.clk(CLOCK), .D(INPUT[14]), .Q(OUTPUT[14]), .preset(SET), .reset(RESET));  // open: Qn, en
  D_Flip_Flop d_ff_16 (.clk(CLOCK), .D(INPUT[15]), .Q(OUTPUT[15]), .preset(SET), .reset(RESET));  // open: Qn, en
endmodule

module UOL (
  input  [7:0] L_INPUT,
  input  OVERFLOW,
  input  [2:0] SELETOR,
  input  CLOCK,
  output BOOLEAN
);

  wire and_1_out, and_2_out, and_3_out, multiplexer_1_out, nand_1_out, not_1_out, not_2_out, not_3_out,
       not_4_out, not_5_out, not_6_out, not_7_out, not_8_out, not_9_out, not_10_out, not_11_out, or_1_out,
       or_2_out;

  and and_1 (and_1_out, L_INPUT[0], L_INPUT[1], L_INPUT[2], L_INPUT[3], L_INPUT[4], L_INPUT[5], L_INPUT[6], L_INPUT[7]);
  or or_1 (or_1_out, L_INPUT[0], L_INPUT[1], L_INPUT[2], L_INPUT[3], L_INPUT[4], L_INPUT[5], L_INPUT[6], L_INPUT[7]);
  not not_1 (not_1_out, L_INPUT[0]);
  not not_2 (not_2_out, L_INPUT[1]);
  not not_3 (not_3_out, L_INPUT[2]);
  not not_4 (not_4_out, L_INPUT[3]);
  and and_2 (and_2_out, not_1_out, not_2_out, not_3_out, not_4_out, not_5_out, not_6_out, not_7_out, not_8_out);
  not not_5 (not_5_out, L_INPUT[4]);
  not not_6 (not_6_out, L_INPUT[5]);
  not not_7 (not_7_out, L_INPUT[6]);
  not not_8 (not_8_out, L_INPUT[7]);
  not not_9 (not_9_out, OVERFLOW);
  nand nand_1 (nand_1_out, L_INPUT[0], L_INPUT[1], L_INPUT[2], L_INPUT[3], L_INPUT[4], L_INPUT[5], L_INPUT[6], L_INPUT[7]);
  and and_3 (and_3_out, not_9_out, or_1_out);
  or or_2 (or_2_out, OVERFLOW, and_2_out);
  not not_10 (not_10_out, OVERFLOW);
  not not_11 (not_11_out, L_INPUT[0]);
  Multiplexer #(.select(3)) multiplexer_1 (
    .in0(and_1_out), .in1(nand_1_out), .in2(and_3_out), .in3(not_10_out), .in4(OVERFLOW), .in5(or_2_out),
    .in6(not_11_out), .in7(L_INPUT[0]), .out(multiplexer_1_out), .sel(SELETOR));  // open: en
  and and_4 (BOOLEAN, CLOCK, multiplexer_1_out);

  // Notes on the sheet:
  //   000: IGUAL
  //   001: DIFERENTE
  //   010: MAIOR
  //   011: MAIOR OU IGUAL
  //   100: MENOR
  //   101: MENOR OU IGUAL
  //   110: PAR
  //   111: IMPAR
endmodule
