// Logisim project Projeto Final - Processador.circ as structural Verilog: 11 circuits, main circuit Processador
module ULA___Controle (
  input  [1:0] A_B,
  input  [1:0] SA_SB,
  input  [2:0] SELETOR,
  input  Cin,
  input  CinShiftE,
  input  CinShiftD,
  output S,
  output Cout,
  output CoutShiftE,
  output CoutShiftD
);

  wire adder_1_cout, adder_1_out, and_1_out, and_2_out, and_3_out, and_4_out, and_5_out, not_1_out,
       not_2_out, not_3_out, not_4_out, or_1_out, or_2_out, or_3_out, subtractor_1_bout, subtractor_1_out,
       xnor_1_out, xor_1_out;

  // Probe on A_B[0]
  // Probe on A_B[1]
  not not_1 (not_1_out, SA_SB[0]);
  not not_2 (not_2_out, A_B[0]);
  not not_3 (not_3_out, SA_SB[1]);
  not not_4 (not_4_out, A_B[1]);
  and and_1 (and_1_out, not_1_out, A_B[0]);
  and and_2 (and_2_out, SA_SB[0], not_2_out);
  and and_3 (and_3_out, not_3_out, A_B[1]);
  and and_4 (and_4_out, SA_SB[1], not_4_out);
  or or_1 (or_1_out, and_1_out, and_2_out);
  or or_2 (or_2_out, and_3_out, and_4_out);
  and and_5 (and_5_out, or_1_out, or_2_out);
  or or_3 (or_3_out, or_1_out, or_2_out);
  xor xor_1 (xor_1_out, or_1_out, or_2_out);
  Adder #(.width(1)) adder_1 (.a(or_1_out), .b(or_2_out), .out(adder_1_out), .cin(Cin), .cout(adder_1_cout));
  Subtractor #(.width(1)) subtractor_1 (
    .a(or_1_out), .b(or_2_out), .out(subtractor_1_out), .bin(Cin), .bout(subtractor_1_bout));
  xnor xnor_1 (xnor_1_out, or_1_out, or_2_out);
  Multiplexer #(.select(3)) multiplexer_1 (
    .in0(and_5_out), .in1(or_3_out), .in2(xor_1_out), .in3(xnor_1_out), .in4(adder_1_out),
    .in5(subtractor_1_out), .in6(CinShiftE), .in7(CinShiftD), .out(S), .sel(SELETOR));  // open: en
  Multiplexer #(.select(3)) multiplexer_2 (
    .in0(1'b0), .in1(1'b0), .in2(1'b0), .in3(1'b0), .in4(adder_1_cout), .in5(subtractor_1_bout), .in6(1'b0),
    .in7(1'b0), .out(Cout), .sel(SELETOR));  // open: en
  Multiplexer #(.select(3)) multiplexer_3 (
    .in0(1'b0), .in1(1'b0), .in2(1'b0), .in3(1'b0), .in4(1'b0), .in5(1'b0), .in6(A_B[0]), .in7(1'b0),
    .out(CoutShiftE), .sel(SELETOR));  // open: en
  Multiplexer #(.select(3)) multiplexer_4 (
    .in0(1'b0), .in1(1'b0), .in2(1'b0), .in3(1'b0), .in4(1'b0), .in5(1'b0), .in6(1'b0), .in7(A_B[0]),
    .out(CoutShiftD), .sel(SELETOR));  // open: en

  // Notes on the sheet:
  //   0
  //   1
  //   0
  //   1
endmodule

module ULA_8_bits (
  input  [4:0] SELETOR,
  input  [7:0] A,
  input  [7:0] B,
  output OVERFLOW,
  output [7:0] S
);

  wire ula_controle_1_cout, ula_controle_1_coutshifte, ula_controle_2_cout, ula_controle_2_coutshifte,
       ula_controle_3_cout, ula_controle_3_coutshiftd, ula_controle_3_coutshifte, ula_controle_4_cout,
       ula_controle_4_coutshiftd, ula_controle_4_coutshifte, ula_controle_5_cout, ula_controle_5_coutshiftd,
       ula_controle_5_coutshifte, ula_controle_6_cout, ula_controle_6_coutshiftd, ula_controle_6_coutshifte,
       ula_controle_7_cout, ula_controle_7_coutshiftd, ula_controle_8_coutshiftd;

  ULA___Controle ula_controle_1 (
    .S(S[0]), .Cout(ula_controle_1_cout), .A_B({B[0], A[0]}), .SA_SB({SELETOR[3], SELETOR[4]}), .Cin(1'b0),
    .SELETOR(SELETOR[2:0]), .CoutShiftE(ula_controle_1_coutshifte), .CinShiftE(1'b0),
    .CinShiftD(ula_controle_3_coutshiftd));  // open: CoutShiftD
  ULA___Controle ula_controle_2 (
    .S(S[1]), .Cout(ula_controle_2_cout), .A_B({B[1], A[1]}), .SA_SB({SELETOR[3], SELETOR[4]}),
    .Cin(ula_controle_1_cout), .SELETOR(SELETOR[2:0]), .CoutShiftE(ula_controle_2_coutshifte),
    .CinShiftE(1'b0), .CinShiftD(ula_controle_4_coutshiftd));  // open: CoutShiftD
  ULA___Controle ula_controle_3 (
    .S(S[2]), .Cout(ula_controle_3_cout), .A_B({B[2], A[2]}), .SA_SB({SELETOR[3], SELETOR[4]}),
    .Cin(ula_controle_2_cout), .SELETOR(SELETOR[2:0]), .CoutShiftE(ula_controle_3_coutshifte),
    .CinShiftE(ula_controle_1_coutshifte), .CinShiftD(ula_controle_5_coutshiftd),
    .CoutShiftD(ula_controle_3_coutshiftd));
  ULA___Controle ula_controle_4 (
    .S(S[3]), .Cout(ula_controle_4_cout), .A_B({B[3], A[3]}), .SA_SB({SELETOR[3], SELETOR[4]}),
    .Cin(ula_controle_3_cout), .SELETOR(SELETOR[2:0]), .CoutShiftE(ula_controle_4_coutshifte),
    .CinShiftE(ula_controle_2_coutshifte), .CinShiftD(ula_controle_6_coutshiftd),
    .CoutShiftD(ula_controle_4_coutshiftd));
  ULA___Controle ula_controle_5 (
    .S(S[4]), .Cout(ula_controle_5_cout), .A_B({B[4], A[4]}), .SA_SB({SELETOR[3], SELETOR[4]}),
    .Cin(ula_controle_4_cout), .SELETOR(SELETOR[2:0]), .CoutShiftE(ula_controle_5_coutshifte),
    .CinShiftE(ula_controle_3_coutshifte), .CinShiftD(ula_controle_7_coutshiftd),
    .CoutShiftD(ula_controle_5_coutshiftd));
  ULA___Controle ula_controle_6 (
    .S(S[5]), .Cout(ula_controle_6_cout), .A_B({B[5], A[5]}), .SA_SB({SELETOR[3], SELETOR[4]}),
    .Cin(ula_controle_5_cout), .SELETOR(SELETOR[2:0]), .CoutShiftE(ula_controle_6_coutshifte),
    .CinShiftE(ula_controle_4_coutshifte), .CinShiftD(ula_controle_8_coutshiftd),
    .CoutShiftD(ula_controle_6_coutshiftd));
  ULA___Controle ula_controle_7 (
    .S(S[6]), .Cout(ula_controle_7_cout), .A_B({B[6], A[6]}), .SA_SB({SELETOR[3], SELETOR[4]}),
    .Cin(ula_controle_6_cout), .SELETOR(SELETOR[2:0]), .CinShiftE(ula_controle_5_coutshifte),
    .CinShiftD(1'b0), .CoutShiftD(ula_controle_7_coutshiftd));  // open: CoutShiftE
  ULA___Controle ula_controle_8 (
    .S(S[7]), .Cout(OVERFLOW), .A_B({B[7], A[7]}), .SA_SB({SELETOR[3], SELETOR[4]}),
    .Cin(ula_controle_7_cout), .SELETOR(SELETOR[2:0]), .CinShiftE(ula_controle_6_coutshifte),
    .CinShiftD(1'b0), .CoutShiftD(ula_controle_8_coutshiftd));  // open: CoutShiftE

  // Notes on the sheet:
  //   00000: E
  //   00001: OU
  //   00010: XOR
  //   00011: XNOR
  //   11000: NÃO OU
  //   11001: NÃO E
  //   10100: NÂO
  //   00100: SOMA
  //   00101: SUB
  //   00110: SHIF E. 
  //   00111: SHIF D.
endmodule

module Processador (
  input  LOAD,
  input  [15:0] Ln0,
  input  [15:0] Ln1,
  input  [15:0] Ln2,
  input  [15:0] Ln3,
  input  [15:0] Ln4,
  input  [15:0] Ln5,
  input  [15:0] Ln6,
  input  RESET,
  input  [15:0] Ln7,
  input  [15:0] Ln8,
  input  [15:0] Ln9,
  input  [15:0] Ln10,
  input  [15:0] Ln11,
  input  [15:0] Ln12,
  input  [15:0] Ln13,
  input  [15:0] Ln14,
  input  [15:0] Ln15,
  output [7:0] PRINT
);

  wire clock_1_out, or_1_out, ula_8_bits_1_overflow, unic_1_clock_mem, unic_1_colck_br, unic_1_ctr_br,
       unic_1_ctr_mem, unic_1_ctr_uol, unic_1_jump, unic_1_out, uol_1_boolean;
  wire [1:0] unic_1_mula, unic_1_muva;
  wire [2:0] unic_1_out_10;
  wire [3:0] multiplexer_1_out, pc_1_out_21, unic_1_end1;
  wire [4:0] unic_1_ula_op;
  wire [7:0] banco_de_registradores_1_out_8, banco_de_registradores_1_out_10,
       banco_de_registradores_1_out_11, banco_de_registradores_1_out_13, banco_de_registradores_1_r1,
       banco_de_registradores_1_r2, \memória_ram_1_output , multiplexer_2_out, multiplexer_3_out,
       pc_1_out_22, pc_1_out_23, ula_8_bits_1_s;

  // Probe on pc_1_out_21
  PC pc_1 (
    .CLOCK(clock_1_out), .in_5(Ln0), .in_6(Ln1), .in_7(Ln2), .in_8(Ln3), .in_9(Ln4), .in_10(Ln5),
    .in_11(Ln6), .in_12(Ln7), .in_13(Ln8), .in_14(Ln9), .in_15(Ln10), .in_16(Ln11), .in_17(Ln12),
    .in_18(Ln13), .in_19(Ln14), .in_20(Ln15), .LOAD(LOAD), .JUMP(or_1_out), .JUMP_END(multiplexer_1_out),
    .out_22(pc_1_out_22), .out_23(pc_1_out_23), .out_21(pc_1_out_21));
  Clock clock_1 (.out(clock_1_out));
  or or_1 (or_1_out, uol_1_boolean, unic_1_jump);
  Multiplexer #(.width(4)) multiplexer_1 (
    .in0(unic_1_end1), .in1(pc_1_out_23[3:0]), .out(multiplexer_1_out), .sel(uol_1_boolean));  // open: en
  \Memória_ROM  \memória_rom_1  (
    .ESC_0_LER_1(1'b0), .ATUAL_OP(pc_1_out_22), .CLOCK(clock_1_out));  // open: ÚLTIMO_OP, RESET, SET
  Multiplexer #(.select(2), .width(8)) multiplexer_2 (
    .in0(pc_1_out_23), .in1(ula_8_bits_1_s), .in2(\memória_ram_1_output ), .out(multiplexer_2_out),
    .sel(unic_1_muva));  // open: in3, en
  UNIC unic_1 (
    .CLOCK(clock_1_out), .OP(pc_1_out_22), .COLCK_BR(unic_1_colck_br), .END1(unic_1_end1[1:0]),
    .END2(unic_1_end1[3:2]), .ULA_OP(unic_1_ula_op), .Ctr_BR(unic_1_ctr_br), .MULA(unic_1_mula),
    .MUVA(unic_1_muva), .CLOCK_MEM(unic_1_clock_mem), .Ctr_MEM(unic_1_ctr_mem), .JUMP(unic_1_jump),
    .out_10(unic_1_out_10), .Ctr_UOL(unic_1_ctr_uol), .OUT(unic_1_out));
  // Probe on banco_de_registradores_1_out_8
  // Probe on banco_de_registradores_1_out_10
  // Probe on banco_de_registradores_1_out_11
  // Probe on banco_de_registradores_1_out_13
  Banco_de_Registradores banco_de_registradores_1 (
    .\ENDEREÇO_R1 (unic_1_end1[1:0]), .\ENDEREÇO_R2 (unic_1_end1[3:2]), .R1(banco_de_registradores_1_r1),
    .R2(banco_de_registradores_1_r2), .ESC_0_LER_1(unic_1_ctr_br), .INPUT(multiplexer_2_out),
    .CLOCK(unic_1_colck_br), .RESET(RESET), .out_8(banco_de_registradores_1_out_8),
    .out_11(banco_de_registradores_1_out_11), .out_10(banco_de_registradores_1_out_10),
    .out_13(banco_de_registradores_1_out_13));  // open: SET
  \Memória_RAM  \memória_ram_1  (
    .OUTPUT(\memória_ram_1_output ), .ARRAY(unic_1_end1[3:2]), .RESET(RESET), .INPUT(multiplexer_2_out),
    .LER_0_ESC_1(unic_1_ctr_mem), .CLOCK(unic_1_clock_mem), .INDEX(pc_1_out_23));  // open: SET
  Multiplexer #(.select(2), .width(8)) multiplexer_3 (
    .in0({8{1'b0}}), .in1(pc_1_out_23), .in2(banco_de_registradores_1_r2), .in3({8{1'b0}}),
    .out(multiplexer_3_out), .sel(unic_1_mula));  // open: en
  ULA_8_bits ula_8_bits_1 (
    .SELETOR(unic_1_ula_op), .A(banco_de_registradores_1_r1), .B(multiplexer_3_out),
    .OVERFLOW(ula_8_bits_1_overflow), .S(ula_8_bits_1_s));
  // Probe on banco_de_registradores_1_r1
  // Probe on multiplexer_3_out
  // Probe on ula_8_bits_1_s
  UOL uol_1 (
    .BOOLEAN(uol_1_boolean), .L_INPUT(ula_8_bits_1_s), .OVERFLOW(ula_8_bits_1_overflow),
    .SELETOR(unic_1_out_10), .CLOCK(unic_1_ctr_uol));
  Multiplexer #(.width(8)) multiplexer_4 (
    .in0({8{1'b0}}), .in1(ula_8_bits_1_s), .out(PRINT), .sel(unic_1_out));  // open: en
endmodule

module \Valor_de_Memória_8_bits  (
  input  CLOCK,
  input  [7:0] INPUT,
  input  SET,
  input  RESET,
  output [7:0] OUTPUT
);

  D_Flip_Flop d_ff_1 (.clk(CLOCK), .D(INPUT[0]), .Q(OUTPUT[0]), .preset(SET), .reset(RESET));  // open: Qn, en
  D_Flip_Flop d_ff_2 (.clk(CLOCK), .D(INPUT[1]), .Q(OUTPUT[1]), .preset(SET), .reset(RESET));  // open: Qn, en
  D_Flip_Flop d_ff_3 (.clk(CLOCK), .D(INPUT[2]), .Q(OUTPUT[2]), .preset(SET), .reset(RESET));  // open: Qn, en
  D_Flip_Flop d_ff_4 (.clk(CLOCK), .D(INPUT[3]), .Q(OUTPUT[3]), .preset(SET), .reset(RESET));  // open: Qn, en
  D_Flip_Flop d_ff_5 (.clk(CLOCK), .D(INPUT[4]), .Q(OUTPUT[4]), .preset(SET), .reset(RESET));  // open: Qn, en
  D_Flip_Flop d_ff_6 (.clk(CLOCK), .D(INPUT[5]), .Q(OUTPUT[5]), .preset(SET), .reset(RESET));  // open: Qn, en
  D_Flip_Flop d_ff_7 (.clk(CLOCK), .D(INPUT[6]), .Q(OUTPUT[6]), .preset(SET), .reset(RESET));  // open: Qn, en
  D_Flip_Flop d_ff_8 (.clk(CLOCK), .D(INPUT[7]), .Q(OUTPUT[7]), .preset(SET), .reset(RESET));  // open: Qn, en
endmodule

module \Memória_ROM  (
  input  RESET,
  input  ESC_0_LER_1,
  input  SET,
  input  [7:0] ATUAL_OP,
  input  CLOCK,
  output [7:0] \ÚLTIMO_OP 
);

  wire demultiplexer_1_out0, demultiplexer_1_out1, demultiplexer_1_out2, demultiplexer_1_out3,
       demultiplexer_1_out4, demultiplexer_1_out5, demultiplexer_1_out6, demultiplexer_1_out7,
       demultiplexer_1_out8, demultiplexer_1_out9, demultiplexer_1_out10, demultiplexer_1_out11,
       demultiplexer_1_out12, demultiplexer_1_out13, demultiplexer_1_out14, demultiplexer_1_out15,
       multiplexer_1_out;
  wire [3:0] counter_1_q, subtractor_1_out;
  wire [7:0] multiplexer_2_out, \valor_de_memória_8_bits_1_output , \valor_de_memória_8_bits_2_output ,
       \valor_de_memória_8_bits_3_output , \valor_de_memória_8_bits_4_output ,
       \valor_de_memória_8_bits_5_output , \valor_de_memória_8_bits_6_output ,
       \valor_de_memória_8_bits_7_output , \valor_de_memória_8_bits_8_output ,
       \valor_de_memória_8_bits_9_output , \valor_de_memória_8_bits_10_output ,
       \valor_de_memória_8_bits_11_output , \valor_de_memória_8_bits_12_output ,
       \valor_de_memória_8_bits_13_output , \valor_de_memória_8_bits_14_output ,
       \valor_de_memória_8_bits_15_output , \valor_de_memória_8_bits_16_output ;

  Counter #(.width(4), .max('hf)) counter_1 (
    .count(1'b1), .Q(counter_1_q), .clk(multiplexer_1_out), .clr(RESET));  // open: load, D, carry
  Multiplexer multiplexer_1 (.in0(CLOCK), .in1(1'b0), .out(multiplexer_1_out), .sel(ESC_0_LER_1));  // open: en
  Demultiplexer #(.select(4)) demultiplexer_1 (
    .out0(demultiplexer_1_out0), .out1(demultiplexer_1_out1), .out2(demultiplexer_1_out2),
    .out3(demultiplexer_1_out3), .out4(demultiplexer_1_out4), .out5(demultiplexer_1_out5),
    .out6(demultiplexer_1_out6), .out7(demultiplexer_1_out7), .out8(demultiplexer_1_out8),
    .out9(demultiplexer_1_out9), .out10(demultiplexer_1_out10), .out11(demultiplexer_1_out11),
    .out12(demultiplexer_1_out12), .out13(demultiplexer_1_out13), .out14(demultiplexer_1_out14),
    .out15(demultiplexer_1_out15), .in(1'b1), .sel(counter_1_q));  // open: en
  Subtractor #(.width(4)) subtractor_1 (.a(counter_1_q), .b(4'b0001), .out(subtractor_1_out));  // open: bin, bout
  \Valor_de_Memória_8_bits  \valor_de_memória_8_bits_1  (
    .INPUT(ATUAL_OP), .SET(SET), .CLOCK(demultiplexer_1_out0), .RESET(RESET),
    .OUTPUT(\valor_de_memória_8_bits_1_output ));
  \Valor_de_Memória_8_bits  \valor_de_memória_8_bits_2  (
    .INPUT(ATUAL_OP), .SET(SET), .CLOCK(demultiplexer_1_out1), .RESET(RESET),
    .OUTPUT(\valor_de_memória_8_bits_2_output ));
  \Valor_de_Memória_8_bits  \valor_de_memória_8_bits_3  (
    .INPUT(ATUAL_OP), .SET(SET), .CLOCK(demultiplexer_1_out2), .RESET(RESET),
    .OUTPUT(\valor_de_memória_8_bits_3_output ));
  \Valor_de_Memória_8_bits  \valor_de_memória_8_bits_4  (
    .INPUT(ATUAL_OP), .SET(SET), .CLOCK(demultiplexer_1_out3), .RESET(RESET),
    .OUTPUT(\valor_de_memória_8_bits_4_output ));
  \Valor_de_Memória_8_bits  \valor_de_memória_8_bits_5  (
    .INPUT(ATUAL_OP), .SET(SET), .CLOCK(demultiplexer_1_out4), .RESET(RESET),
    .OUTPUT(\valor_de_memória_8_bits_5_output ));
  \Valor_de_Memória_8_bits  \valor_de_memória_8_bits_6  (
    .INPUT(ATUAL_OP), .SET(SET), .CLOCK(demultiplexer_1_out5), .RESET(RESET),
    .OUTPUT(\valor_de_memória_8_bits_6_output ));
  \Valor_de_Memória_8_bits  \valor_de_memória_8_bits_7  (
    .INPUT(ATUAL_OP), .SET(SET), .CLOCK(demultiplexer_1_out6), .RESET(RESET),
    .OUTPUT(\valor_de_memória_8_bits_7_output ));
  \Valor_de_Memória_8_bits  \valor_de_memória_8_bits_8  (
    .INPUT(ATUAL_OP), .SET(SET), .CLOCK(demultiplexer_1_out7), .RESET(RESET),
    .OUTPUT(\valor_de_memória_8_bits_8_output ));
  \Valor_de_Memória_8_bits  \valor_de_memória_8_bits_9  (
    .INPUT(ATUAL_OP), .SET(SET), .CLOCK(demultiplexer_1_out8), .RESET(RESET),
    .OUTPUT(\valor_de_memória_8_bits_9_output ));
  \Valor_de_Memória_8_bits  \valor_de_memória_8_bits_10  (
    .INPUT(ATUAL_OP), .SET(SET), .CLOCK(demultiplexer_1_out9), .RESET(RESET),
    .OUTPUT(\valor_de_memória_8_bits_10_output ));
  \Valor_de_Memória_8_bits  \valor_de_memória_8_bits_11  (
    .INPUT(ATUAL_OP), .SET(SET), .CLOCK(demultiplexer_1_out10), .RESET(RESET),
    .OUTPUT(\valor_de_memória_8_bits_11_output ));
  \Valor_de_Memória_8_bits  \valor_de_memória_8_bits_12  (
    .INPUT(ATUAL_OP), .SET(SET), .CLOCK(demultiplexer_1_out11), .RESET(RESET),
    .OUTPUT(\valor_de_memória_8_bits_12_output ));
  \Valor_de_Memória_8_bits  \valor_de_memória_8_bits_13  (
    .INPUT(ATUAL_OP), .SET(SET), .CLOCK(demultiplexer_1_out12), .RESET(RESET),
    .OUTPUT(\valor_de_memória_8_bits_13_output ));
  \Valor_de_Memória_8_bits  \valor_de_memória_8_bits_14  (
    .INPUT(ATUAL_OP), .SET(SET), .CLOCK(demultiplexer_1_out13), .RESET(RESET),
    .OUTPUT(\valor_de_memória_8_bits_14_output ));
  \Valor_de_Memória_8_bits  \valor_de_memória_8_bits_15  (
    .INPUT(ATUAL_OP), .SET(SET), .CLOCK(demultiplexer_1_out14), .RESET(RESET),
    .OUTPUT(\valor_de_memória_8_bits_15_output ));
  \Valor_de_Memória_8_bits  \valor_de_memória_8_bits_16  (
    .INPUT(ATUAL_OP), .SET(SET), .CLOCK(demultiplexer_1_out15), .RESET(RESET),
    .OUTPUT(\valor_de_memória_8_bits_16_output ));
  // Probe on \valor_de_memória_8_bits_1_output 
  // Probe on \valor_de_memória_8_bits_2_output 
  // Probe on \valor_de_memória_8_bits_3_output 
  // Probe on \valor_de_memória_8_bits_4_output 
  // Probe on \valor_de_memória_8_bits_5_output 
  // Probe on \valor_de_memória_8_bits_6_output 
  // Probe on \valor_de_memória_8_bits_7_output 
  // Probe on \valor_de_memória_8_bits_8_output 
  // Probe on \valor_de_memória_8_bits_9_output 
  // Probe on \valor_de_memória_8_bits_10_output 
  // Probe on \valor_de_memória_8_bits_11_output 
  // Probe on \valor_de_memória_8_bits_12_output 
  // Probe on \valor_de_memória_8_bits_13_output 
  // Probe on \valor_de_memória_8_bits_14_output 
  // Probe on \valor_de_memória_8_bits_15_output 
  // Probe on \valor_de_memória_8_bits_16_output 
  // Probe on subtractor_1_out
  Multiplexer #(.select(4), .width(8)) multiplexer_2 (
    .in0(\valor_de_memória_8_bits_1_output ), .in1(\valor_de_memória_8_bits_2_output ),
    .in2(\valor_de_memória_8_bits_3_output ), .in3(\valor_de_memória_8_bits_4_output ),
    .in4(\valor_de_memória_8_bits_5_output ), .in5(\valor_de_memória_8_bits_6_output ),
    .in6(\valor_de_memória_8_bits_7_output ), .in7(\valor_de_memória_8_bits_8_output ),
    .in8(\valor_de_memória_8_bits_9_output ), .in9(\valor_de_memória_8_bits_10_output ),
    .in10(\valor_de_memória_8_bits_11_output ), .in11(\valor_de_memória_8_bits_12_output ),
    .in12(\valor_de_memória_8_bits_13_output ), .in13(\valor_de_memória_8_bits_14_output ),
    .in14(\valor_de_memória_8_bits_15_output ), .in15(\valor_de_memória_8_bits_16_output ),
    .out(multiplexer_2_out), .sel(subtractor_1_out));  // open: en
  Multiplexer #(.width(8)) multiplexer_3 (
    .in0({8{1'b0}}), .in1(multiplexer_2_out), .out(\ÚLTIMO_OP ), .sel(ESC_0_LER_1));  // open: en
endmodule

module Banco_de_Registradores (
  input  ESC_0_LER_1,
  input  RESET,
  input  [7:0] INPUT,
  input  SET,
  input  [1:0] \ENDEREÇO_R1 ,
  input  CLOCK,
  input  [1:0] \ENDEREÇO_R2 ,
  output [7:0] out_8,
  output [7:0] R1,
  output [7:0] out_10,
  output [7:0] out_11,
  output [7:0] R2,
  output [7:0] out_13
);

  wire demultiplexer_1_out0, demultiplexer_1_out1, demultiplexer_1_out2, demultiplexer_1_out3,
       multiplexer_1_out;

  Multiplexer multiplexer_1 (.in0(CLOCK), .in1(1'b0), .out(multiplexer_1_out), .sel(ESC_0_LER_1));  // open: en
  Demultiplexer #(.select(2)) demultiplexer_1 (
    .out0(demultiplexer_1_out0), .out1(demultiplexer_1_out1), .out2(demultiplexer_1_out2),
    .out3(demultiplexer_1_out3), .in(multiplexer_1_out), .sel(\ENDEREÇO_R1 ));  // open: en
  \Valor_de_Memória_8_bits  \valor_de_memória_8_bits_1  (
    .INPUT(INPUT), .SET(SET), .CLOCK(demultiplexer_1_out0), .RESET(RESET), .OUTPUT(out_8));
  \Valor_de_Memória_8_bits  \valor_de_memória_8_bits_2  (
    .INPUT(INPUT), .SET(SET), .CLOCK(demultiplexer_1_out1), .RESET(RESET), .OUTPUT(out_10));
  \Valor_de_Memória_8_bits  \valor_de_memória_8_bits_3  (
    .INPUT(INPUT), .SET(SET), .CLOCK(demultiplexer_1_out2), .RESET(RESET), .OUTPUT(out_11));
  \Valor_de_Memória_8_bits  \valor_de_memória_8_bits_4  (
    .INPUT(INPUT), .SET(SET), .CLOCK(demultiplexer_1_out3), .RESET(RESET), .OUTPUT(out_13));
  Multiplexer #(.select(2), .width(8)) multiplexer_2 (
    .in0(out_8), .in1(out_10), .in2(out_11), .in3(out_13), .out(R1), .sel(\ENDEREÇO_R1 ));  // open: en
  Multiplexer #(.select(2), .width(8)) multiplexer_3 (
    .in0(out_8), .in1(out_10), .in2(out_11), .in3(out_13), .out(R2), .sel(\ENDEREÇO_R2 ));  // open: en
endmodule

module UNIC (
  input  [7:0] OP,
  input  CLOCK,
  output [1:0] MULA,
  output COLCK_BR,
  output [1:0] END1,
  output [1:0] END2,
  output CLOCK_MEM,
  output [4:0] ULA_OP,
  output Ctr_BR,
  output [2:0] out_10,
  output [1:0] MUVA,
  output OUT,
  output Ctr_MEM,
  output JUMP,
  output Ctr_UOL
);

  wire demultiplexer_1_out1, demultiplexer_1_out2, demultiplexer_1_out3, demultiplexer_1_out4,
       demultiplexer_1_out5, demultiplexer_1_out8, demultiplexer_1_out9, demultiplexer_1_out10,
       demultiplexer_1_out11, demultiplexer_1_out12, demultiplexer_1_out13, demultiplexer_1_out14, or_6_out;
  wire [1:0] or_1_out;

  Demultiplexer #(.select(4)) demultiplexer_1 (
    .out0(OUT), .out1(demultiplexer_1_out1), .out2(demultiplexer_1_out2), .out3(demultiplexer_1_out3),
    .out4(demultiplexer_1_out4), .out5(demultiplexer_1_out5), .out6(Ctr_BR), .out7(JUMP),
    .out8(demultiplexer_1_out8), .out9(demultiplexer_1_out9), .out10(demultiplexer_1_out10),
    .out11(demultiplexer_1_out11), .out12(demultiplexer_1_out12), .out13(demultiplexer_1_out13),
    .out14(demultiplexer_1_out14), .out15(MUVA[1]), .in(1'b1), .sel(OP[7:4]));  // open: en
  or or_1 (or_1_out[0], demultiplexer_1_out12, demultiplexer_1_out10, demultiplexer_1_out4, demultiplexer_1_out5, demultiplexer_1_out11, demultiplexer_1_out13);
  or or_2 (MULA[0], demultiplexer_1_out2, demultiplexer_1_out4);
  or or_3 (MULA[1], demultiplexer_1_out3, demultiplexer_1_out5);
  or or_4 (or_1_out[1], demultiplexer_1_out8, demultiplexer_1_out9);
  // Probe on {1'b0, or_1_out}
  Multiplexer #(.select(3), .width(5)) multiplexer_1 (
    .in0(5'b00100), .in1(5'b00101), .in2(5'b00011), .in3({5{1'b0}}), .in4({5{1'b0}}), .in5({5{1'b0}}),
    .in6({5{1'b0}}), .in7({5{1'b0}}), .out(ULA_OP), .sel({1'b0, or_1_out}));  // open: en
  or or_5 (MUVA[0], demultiplexer_1_out2, demultiplexer_1_out3, Ctr_BR, demultiplexer_1_out4, demultiplexer_1_out5);
  and and_1 (COLCK_BR, CLOCK, or_6_out);
  or or_6 (or_6_out, demultiplexer_1_out1, MUVA[1], MUVA[0]);
  and and_2 (CLOCK_MEM, CLOCK, Ctr_BR);
  or or_7 (Ctr_UOL, demultiplexer_1_out8, demultiplexer_1_out9, demultiplexer_1_out10, demultiplexer_1_out11, demultiplexer_1_out12, demultiplexer_1_out13, demultiplexer_1_out14);

  assign Ctr_MEM = Ctr_BR;
  assign END1 = OP[1:0];
  assign END2 = OP[3:2];
  assign out_10 = OP[6:4];
endmodule

module \Memória_RAM  (
  input  [7:0] INDEX,
  input  [1:0] ARRAY,
  input  LER_0_ESC_1,
  input  RESET,
  input  [7:0] INPUT,
  input  SET,
  input  CLOCK,
  output [7:0] OUTPUT
);

  wire demultiplexer_1_out0, demultiplexer_1_out1, demultiplexer_1_out2, demultiplexer_1_out3,
       demultiplexer_1_out4, demultiplexer_1_out5, demultiplexer_1_out6, demultiplexer_1_out7,
       demultiplexer_1_out8, demultiplexer_1_out9, demultiplexer_1_out10, demultiplexer_1_out11,
       demultiplexer_1_out12, demultiplexer_1_out13, demultiplexer_1_out14, demultiplexer_1_out15,
       multiplexer_1_out;
  wire [7:0] multiplexer_2_out, \valor_de_memória_8_bits_1_output , \valor_de_memória_8_bits_2_output ,
       \valor_de_memória_8_bits_3_output , \valor_de_memória_8_bits_4_output ,
       \valor_de_memória_8_bits_5_output , \valor_de_memória_8_bits_6_output ,
       \valor_de_memória_8_bits_7_output , \valor_de_memória_8_bits_8_output ,
       \valor_de_memória_8_bits_9_output , \valor_de_memória_8_bits_10_output ,
       \valor_de_memória_8_bits_11_output , \valor_de_memória_8_bits_12_output ,
       \valor_de_memória_8_bits_13_output , \valor_de_memória_8_bits_14_output ,
       \valor_de_memória_8_bits_15_output , \valor_de_memória_8_bits_16_output ;

  Multiplexer multiplexer_1 (.in0(1'b0), .in1(CLOCK), .out(multiplexer_1_out), .sel(LER_0_ESC_1));  // open: en
  Demultiplexer #(.select(4)) demultiplexer_1 (
    .out0(demultiplexer_1_out0), .out1(demultiplexer_1_out1), .out2(demultiplexer_1_out2),
    .out3(demultiplexer_1_out3), .out4(demultiplexer_1_out4), .out5(demultiplexer_1_out5),
    .out6(demultiplexer_1_out6), .out7(demultiplexer_1_out7), .out8(demultiplexer_1_out8),
    .out9(demultiplexer_1_out9), .out10(demultiplexer_1_out10), .out11(demultiplexer_1_out11),
    .out12(demultiplexer_1_out12), .out13(demultiplexer_1_out13), .out14(demultiplexer_1_out14),
    .out15(demultiplexer_1_out15), .in(multiplexer_1_out), .sel({ARRAY, INDEX[1:0]}));  // open: en
  \Valor_de_Memória_8_bits  \valor_de_memória_8_bits_1  (
    .INPUT(INPUT), .SET(SET), .CLOCK(demultiplexer_1_out0), .RESET(RESET),
    .OUTPUT(\valor_de_memória_8_bits_1_output ));
  // Probe on \valor_de_memória_8_bits_1_output 
  \Valor_de_Memória_8_bits  \valor_de_memória_8_bits_2  (
    .INPUT(INPUT), .SET(SET), .CLOCK(demultiplexer_1_out1), .RESET(RESET),
    .OUTPUT(\valor_de_memória_8_bits_2_output ));
  // Probe on \valor_de_memória_8_bits_2_output 
  \Valor_de_Memória_8_bits  \valor_de_memória_8_bits_3  (
    .INPUT(INPUT), .SET(SET), .CLOCK(demultiplexer_1_out2), .RESET(RESET),
    .OUTPUT(\valor_de_memória_8_bits_3_output ));
  // Probe on \valor_de_memória_8_bits_3_output 
  \Valor_de_Memória_8_bits  \valor_de_memória_8_bits_4  (
    .INPUT(INPUT), .SET(SET), .CLOCK(demultiplexer_1_out3), .RESET(RESET),
    .OUTPUT(\valor_de_memória_8_bits_4_output ));
  // Probe on \valor_de_memória_8_bits_4_output 
  \Valor_de_Memória_8_bits  \valor_de_memória_8_bits_5  (
    .INPUT(INPUT), .SET(SET), .CLOCK(demultiplexer_1_out4), .RESET(RESET),
    .OUTPUT(\valor_de_memória_8_bits_5_output ));
  // Probe on \valor_de_memória_8_bits_5_output 
  \Valor_de_Memória_8_bits  \valor_de_memória_8_bits_6  (
    .INPUT(INPUT), .SET(SET), .CLOCK(demultiplexer_1_out5), .RESET(RESET),
    .OUTPUT(\valor_de_memória_8_bits_6_output ));
  // Probe on \valor_de_memória_8_bits_6_output 
  \Valor_de_Memória_8_bits  \valor_de_memória_8_bits_7  (
    .INPUT(INPUT), .SET(SET), .CLOCK(demultiplexer_1_out6), .RESET(RESET),
    .OUTPUT(\valor_de_memória_8_bits_7_output ));
  // Probe on \valor_de_memória_8_bits_7_output 
  \Valor_de_Memória_8_bits  \valor_de_memória_8_bits_8  (
    .INPUT(INPUT), .SET(SET), .CLOCK(demultiplexer_1_out7), .RESET(RESET),
    .OUTPUT(\valor_de_memória_8_bits_8_output ));
  // Probe on \valor_de_memória_8_bits_8_output 
  \Valor_de_Memória_8_bits  \valor_de_memória_8_bits_9  (
    .INPUT(INPUT), .SET(SET), .CLOCK(demultiplexer_1_out8), .RESET(RESET),
    .OUTPUT(\valor_de_memória_8_bits_9_output ));
  // Probe on \valor_de_memória_8_bits_9_output 
  \Valor_de_Memória_8_bits  \valor_de_memória_8_bits_10  (
    .INPUT(INPUT), .SET(SET), .CLOCK(demultiplexer_1_out9), .RESET(RESET),
    .OUTPUT(\valor_de_memória_8_bits_10_output ));
  // Probe on \valor_de_memória_8_bits_10_output 
  \Valor_de_Memória_8_bits  \valor_de_memória_8_bits_11  (
    .INPUT(INPUT), .SET(SET), .CLOCK(demultiplexer_1_out10), .RESET(RESET),
    .OUTPUT(\valor_de_memória_8_bits_11_output ));
  // Probe on \valor_de_memória_8_bits_11_output 
  \Valor_de_Memória_8_bits  \valor_de_memória_8_bits_12  (
    .INPUT(INPUT), .SET(SET), .CLOCK(demultiplexer_1_out11), .RESET(RESET),
    .OUTPUT(\valor_de_memória_8_bits_12_output ));
  // Probe on \valor_de_memória_8_bits_12_output 
  \Valor_de_Memória_8_bits  \valor_de_memória_8_bits_13  (
    .INPUT(INPUT), .SET(SET), .CLOCK(demultiplexer_1_out12), .RESET(RESET),
    .OUTPUT(\valor_de_memória_8_bits_13_output ));
  // Probe on \valor_de_memória_8_bits_13_output 
  \Valor_de_Memória_8_bits  \valor_de_memória_8_bits_14  (
    .INPUT(INPUT), .SET(SET), .CLOCK(demultiplexer_1_out13), .RESET(RESET),
    .OUTPUT(\valor_de_memória_8_bits_14_output ));
  // Probe on \valor_de_memória_8_bits_14_output 
  \Valor_de_Memória_8_bits  \valor_de_memória_8_bits_15  (
    .INPUT(INPUT), .SET(SET), .CLOCK(demultiplexer_1_out14), .RESET(RESET),
    .OUTPUT(\valor_de_memória_8_bits_15_output ));
  // Probe on \valor_de_memória_8_bits_15_output 
  \Valor_de_Memória_8_bits  \valor_de_memória_8_bits_16  (
    .INPUT(INPUT), .SET(SET), .CLOCK(demultiplexer_1_out15), .RESET(RESET),
    .OUTPUT(\valor_de_memória_8_bits_16_output ));
  // Probe on \valor_de_memória_8_bits_16_output 
  Multiplexer #(.select(4), .width(8)) multiplexer_2 (
    .in0(\valor_de_memória_8_bits_1_output ), .in1(\valor_de_memória_8_bits_2_output ),
    .in2(\valor_de_memória_8_bits_3_output ), .in3(\valor_de_memória_8_bits_4_output ),
    .in4(\valor_de_memória_8_bits_5_output ), .in5(\valor_de_memória_8_bits_6_output ),
    .in6(\valor_de_memória_8_bits_7_output ), .in7(\valor_de_memória_8_bits_8_output ),
    .in8(\valor_de_memória_8_bits_9_output ), .in9(\valor_de_memória_8_bits_10_output ),
    .in10(\valor_de_memória_8_bits_11_output ), .in11(\valor_de_memória_8_bits_12_output ),
    .in12(\valor_de_memória_8_bits_13_output ), .in13(\valor_de_memória_8_bits_14_output ),
    .in14(\valor_de_memória_8_bits_15_output ), .in15(\valor_de_memória_8_bits_16_output ),
    .out(multiplexer_2_out), .sel({ARRAY, INDEX[1:0]}));  // open: en
  Multiplexer #(.width(8)) multiplexer_3 (
    .in0(multiplexer_2_out), .in1({8{1'b0}}), .out(OUTPUT), .sel(LER_0_ESC_1));  // open: en
endmodule

module PC (
  input  LOAD,
  input  [3:0] JUMP_END,
  input  JUMP,
  input  CLOCK,
  input  [15:0] in_5,
  input  [15:0] in_6,
  input  [15:0] in_7,
  input  [15:0] in_8,
  input  [15:0] in_9,
  input  [15:0] in_10,
  input  [15:0] in_11,
  input  [15:0] in_12,
  input  [15:0] in_13,
  input  [15:0] in_14,
  input  [15:0] in_15,
  input  [15:0] in_16,
  input  [15:0] in_17,
  input  [15:0] in_18,
  input  [15:0] in_19,
  input  [15:0] in_20,
  output [3:0] out_21,
  output [7:0] out_22,
  output [7:0] out_23
);

  wire not_1_out, not_2_out;
  wire [15:0] linha_de_comando_16_bits_1_output, linha_de_comando_16_bits_2_output,
       linha_de_comando_16_bits_3_output, linha_de_comando_16_bits_4_output,
       linha_de_comando_16_bits_5_output, linha_de_comando_16_bits_6_output,
       linha_de_comando_16_bits_7_output, linha_de_comando_16_bits_8_output,
       linha_de_comando_16_bits_9_output, linha_de_comando_16_bits_10_output,
       linha_de_comando_16_bits_11_output, linha_de_comando_16_bits_12_output,
       linha_de_comando_16_bits_13_output, linha_de_comando_16_bits_14_output,
       linha_de_comando_16_bits_15_output, linha_de_comando_16_bits_16_output;

  not not_1 (not_1_out, CLOCK);
  Linha_de_Comando_16_bits linha_de_comando_16_bits_1 (
    .INPUT(in_5), .CLOCK(LOAD), .OUTPUT(linha_de_comando_16_bits_1_output));  // open: SET, RESET
  Linha_de_Comando_16_bits linha_de_comando_16_bits_2 (
    .INPUT(in_6), .CLOCK(LOAD), .OUTPUT(linha_de_comando_16_bits_2_output));  // open: SET, RESET
  Linha_de_Comando_16_bits linha_de_comando_16_bits_3 (
    .INPUT(in_7), .CLOCK(LOAD), .OUTPUT(linha_de_comando_16_bits_3_output));  // open: SET, RESET
  Linha_de_Comando_16_bits linha_de_comando_16_bits_4 (
    .INPUT(in_8), .CLOCK(LOAD), .OUTPUT(linha_de_comando_16_bits_4_output));  // open: SET, RESET
  Linha_de_Comando_16_bits linha_de_comando_16_bits_5 (
    .INPUT(in_9), .CLOCK(LOAD), .OUTPUT(linha_de_comando_16_bits_5_output));  // open: SET, RESET
  Linha_de_Comando_16_bits linha_de_comando_16_bits_6 (
    .INPUT(in_10), .CLOCK(LOAD), .OUTPUT(linha_de_comando_16_bits_6_output));  // open: SET, RESET
  Linha_de_Comando_16_bits linha_de_comando_16_bits_7 (
    .INPUT(in_11), .CLOCK(LOAD), .OUTPUT(linha_de_comando_16_bits_7_output));  // open: SET, RESET
  Linha_de_Comando_16_bits linha_de_comando_16_bits_8 (
    .INPUT(in_12), .CLOCK(LOAD), .OUTPUT(linha_de_comando_16_bits_8_output));  // open: SET, RESET
  Linha_de_Comando_16_bits linha_de_comando_16_bits_9 (
    .INPUT(in_13), .CLOCK(LOAD), .OUTPUT(linha_de_comando_16_bits_9_output));  // open: SET, RESET
  Linha_de_Comando_16_bits linha_de_comando_16_bits_10 (
    .INPUT(in_14), .CLOCK(LOAD), .OUTPUT(linha_de_comando_16_bits_10_output));  // open: SET, RESET
  Linha_de_Comando_16_bits linha_de_comando_16_bits_11 (
    .INPUT(in_15), .CLOCK(LOAD), .OUTPUT(linha_de_comando_16_bits_11_output));  // open: SET, RESET
  Linha_de_Comando_16_bits linha_de_comando_16_bits_12 (
    .INPUT(in_16), .CLOCK(LOAD), .OUTPUT(linha_de_comando_16_bits_12_output));  // open: SET, RESET
  Linha_de_Comando_16_bits linha_de_comando_16_bits_13 (
    .INPUT(in_17), .CLOCK(LOAD), .OUTPUT(linha_de_comando_16_bits_13_output));  // open: SET, RESET
  Linha_de_Comando_16_bits linha_de_comando_16_bits_14 (
    .INPUT(in_18), .CLOCK(LOAD), .OUTPUT(linha_de_comando_16_bits_14_output));  // open: SET, RESET
  Linha_de_Comando_16_bits linha_de_comando_16_bits_15 (
    .INPUT(in_19), .CLOCK(LOAD), .OUTPUT(linha_de_comando_16_bits_15_output));  // open: SET, RESET
  Linha_de_Comando_16_bits linha_de_comando_16_bits_16 (
    .INPUT(in_20), .CLOCK(LOAD), .OUTPUT(linha_de_comando_16_bits_16_output));  // open: SET, RESET
  not not_2 (not_2_out, JUMP);
  Counter #(.width(4), .max('hf)) counter_1 (
    .load(JUMP), .D(JUMP_END), .count(not_2_out), .Q(out_21), .clk(not_1_out));  // open: carry, clr
  Multiplexer #(.select(4), .width(16)) multiplexer_1 (
    .in0(linha_de_comando_16_bits_1_output), .in1(linha_de_comando_16_bits_2_output),
    .in2(linha_de_comando_16_bits_3_output), .in3(linha_de_comando_16_bits_4_output),
    .in4(linha_de_comando_16_bits_5_output), .in5(linha_de_comando_16_bits_6_output),
    .in6(linha_de_comando_16_bits_7_output), .in7(linha_de_comando_16_bits_8_output),
    .in8(linha_de_comando_16_bits_9_output), .in9(linha_de_comando_16_bits_10_output),
    .in10(linha_de_comando_16_bits_11_output), .in11(linha_de_comando_16_bits_12_output),
    .in12(linha_de_comando_16_bits_13_output), .in13(linha_de_comando_16_bits_14_output),
    .in14(linha_de_comando_16_bits_15_output), .in15(linha_de_comando_16_bits_16_output),
    .out({out_23, out_22}), .sel(out_21));  // open: en
endmodule

module Linha_de_Comando_16_bits (
  input  CLOCK,
  input  [15:0] INPUT,
  input  SET,
  input  RESET,
  output [15:0] OUTPUT
);

  D_Flip_Flop d_ff_1 (.clk(CLOCK), .D(INPUT[0]), .Q(OUTPUT[0]), .preset(SET), .reset(RESET));  // open: Qn, en
  D_Flip_Flop d_ff_2 (.clk(CLOCK), .D(INPUT[1]), .Q(OUTPUT[1]), .preset(SET), .reset(RESET));  // open: Qn, en
  D_Flip_Flop d_ff_3 (.clk(CLOCK), .D(INPUT[2]), .Q(OUTPUT[2]), .preset(SET), .reset(RESET));  // open: Qn, en
  D_Flip_Flop d_ff_4 (.clk(CLOCK), .D(INPUT[3]), .Q(OUTPUT[3]), .preset(SET), .reset(RESET));  // open: Qn, en
  D_Flip_Flop d_ff_5 (.clk(CLOCK), .D(INPUT[4]), .Q(OUTPUT[4]), .preset(SET), .reset(RESET));  // open: Qn, en
  D_Flip_Flop d_ff_6 (.clk(CLOCK), .D(INPUT[5]), .Q(OUTPUT[5]), .preset(SET), .reset(RESET));  // open: Qn, en
  D_Flip_Flop d_ff_7 (.clk(CLOCK), .D(INPUT[6]), .Q(OUTPUT[6]), .preset(SET), .reset(RESET));  // open: Qn, en
  D_Flip_Flop d_ff_8 (.clk(CLOCK), .D(INPUT[7]), .Q(OUTPUT[7]), .preset(SET), .reset(RESET));  // open: Qn, en
  D_Flip_Flop d_ff_9 (.clk(CLOCK), .D(INPUT[8]), .Q(OUTPUT[8]), .preset(SET), .reset(RESET));  // open: Qn, en
  D_Flip_Flop d_ff_10 (.clk(CLOCK), .D(INPUT[9]), .Q(OUTPUT[9]), .preset(SET), .reset(RESET));  // open: Qn, en
  D_Flip_Flop d_ff_11 (.clk(CLOCK), .D(INPUT[10]), .Q(OUTPUT[10]), .preset(SET), .reset(RESET));  // open: Qn, en
  D_Flip_Flop d_ff_12 (.clk(CLOCK), .D(INPUT[11]), .Q(OUTPUT[11]), .preset(SET), .reset(RESET));  // open: Qn, en
  D_Flip_Flop d_ff_13 (.clk(CLOCK), .D(INPUT[12]), .Q(OUTPUT[12]), .preset(SET), .reset(RESET));  // open: Qn, en
  D_Flip_Flop d_ff_14 (.clk(CLOCK), .D(INPUT[13]), .Q(OUTPUT[13]), .preset(SET), .reset(RESET));  // open: Qn, en
  D_Flip_Flop d_ff_15 (.clk(CLOCK), .D(INPUT[14]), .Q(OUTPUT[14]), .preset(SET), .reset(RESET));  // open: Qn, en
  D_Flip_Flop d_ff_16 (.clk(CLOCK), .D(INPUT[15]), .Q(OUTPUT[15]), .preset(SET), .reset(RESET));  // open: Qn, en
endmodule

module UOL (
  input  [7:0] L_INPUT,
  input  OVERFLOW,
  input  [2:0] SELETOR,
  input  CLOCK,
  output BOOLEAN
);

  wire and_1_out, and_2_out, and_3_out, multiplexer_1_out, nand_1_out, not_1_out, not_2_out, not_3_out,
       not_4_out, not_5_out, not_6_out, not_7_out, not_8_out, not_9_out, not_10_out, not_11_out, or_1_out,
       or_2_out;

  and and_1 (and_1_out, L_INPUT[0], L_INPUT[1], L_INPUT[2], L_INPUT[3], L_INPUT[4], L_INPUT[5], L_INPUT[6], L_INPUT[7]);
  or or_1 (or_1_out, L_INPUT[0], L_INPUT[1], L_INPUT[2], L_INPUT[3], L_INPUT[4], L_INPUT[5], L_INPUT[6], L_INPUT[7]);
  not not_1 (not_1_out, L_INPUT[0]);
  not not_2 (not_2_out, L_INPUT[1]);
  not not_3 (not_3_out, L_INPUT[2]);
  not not_4 (not_4_out, L_INPUT[3]);
  and and_2 (and_2_out, not_1_out, not_2_out, not_3_out, not_4_out, not_5_out, not_6_out, not_7_out, not_8_out);
  not not_5 (not_5_out, L_INPUT[4]);
  not not_6 (not_6_out, L_INPUT[5]);
  not not_7 (not_7_out, L_INPUT[6]);
  not not_8 (not_8_out, L_INPUT[7]);
  not not_9 (not_9_out, OVERFLOW);
  nand nand_1 (nand_1_out, L_INPUT[0], L_INPUT[1], L_INPUT[2], L_INPUT[3], L_INPUT[4], L_INPUT[5], L_INPUT[6], L_INPUT[7]);
  and and_3 (and_3_out, not_9_out, or_1_out);
  or or_2 (or_2_out, OVERFLOW, and_2_out);
  not not_10 (not_10_out, OVERFLOW);
  not not_11 (not_11_out, L_INPUT[0]);
  Multiplexer #(.select(3)) multiplexer_1 (
    .in0(and_1_out), .in1(nand_1_out), .in2(and_3_out), .in3(not_10_out), .in4(OVERFLOW), .in5(or_2_out),
    .in6(not_11_out), .in7(L_INPUT[0]), .out(multiplexer_1_out), .sel(SELETOR));  // open: en
  and and_4 (BOOLEAN, CLOCK, multiplexer_1_out);
endmodule
